// Logisim project RiscV_Pipeline_hdl.circ as structural Verilog: 17 circuits, main circuit main
module main (
  output halt,
  output STALL,
  output FLUSH,
  output [31:0] PC_out,
  output [31:0] cycles
);

  wire and_1_out, branchunit_1_cond, clk, d_UseRs1, d_UseRs2, e_Branch, e_BSel, e_Jal, e_Jalr, e_MemRead,
       e_rdnz, e_ResPC4, fm1, fm2, fw1, fw2, m_MemWrite, m_RegWrite, pcen, w_MemRead, w_RegWrite, wb_byp1,
       wb_byp2;
  wire [1:0] e_ASel, m_boff;
  wire [2:0] d_f3, e_f3, m_f3, maincontrol_1_d_immsel;
  wire [3:0] e_ALUOp;
  wire [4:0] d_rd, d_rs1, d_rs2, e_rd, e_rs1, e_rs2, m_rd, w_rd;
  wire [19:0] d_ctrl, d_ctrl_q, e_ctrl, m_ctrl;
  wire [31:0] alu_1_y, d_imm, d_instr, d_pc, e_brt, e_imm, e_jalrt, e_pc, e_pc4, e_target, ex_mem_1_m_r2, fb,
       id_ex_1_e_r1, id_ex_1_e_r2, IMEM_data, loadunit_1_v, m_mraw, mem_wb_1_w_res, multiplexer_1_out,
       multiplexer_2_out, multiplexer_3_out, multiplexer_4_out, multiplexer_5_out, multiplexer_6_out,
       multiplexer_7_out, multiplexer_9_out, multiplexer_10_out, multiplexer_11_out, pc4f, regfile_1_r1,
       regfile_1_r2, storeunit_1_new, w_data, w_mdata;
  wire [31:2] m_res;

  Multiplexer #(.width(32), .select(1)) multiplexer_1 (
    .in0(pc4f), .in1(e_target), .out(multiplexer_1_out), .sel(FLUSH));
  CycleCounter cyclecounter_1 (.clk(clk), .cycles(cycles));
  Clock clock_1 (.out(clk));
  Register #(.width(32)) register_1 (.D(multiplexer_1_out), .en(pcen), .clk(clk), .Q(PC_out));  // open: clr
  Adder #(.width(32)) adder_1 (.a(PC_out), .b(32'h4), .out(pc4f));  // open: cin, cout
  ROM #(.addrWidth(10), .dataWidth(32)) IMEM (.addr(PC_out[11:2]), .data(IMEM_data));
  Multiplexer #(.width(32), .select(1)) multiplexer_2 (
    .in0(IMEM_data), .in1({32{1'b0}}), .out(multiplexer_2_out), .sel(FLUSH));
  IF_ID if_id_1 (.clk(clk), .f_instr_q(multiplexer_2_out), .pc(PC_out), .pcen(pcen), .d_instr(d_instr), .d_pc(d_pc));
  InstrDecode instrdecode_1 (.d_instr(d_instr), .d_f3(d_f3), .d_rd(d_rd), .d_rs1(d_rs1), .d_rs2(d_rs2));
  MainControl maincontrol_1 (
    .d_instr(d_instr), .d_ImmSel(maincontrol_1_d_immsel), .d_UseRs1(d_UseRs1), .d_UseRs2(d_UseRs2),
    .d_ctrl(d_ctrl));
  HazardUnit hazardunit_1 (
    .d_UseRs1(d_UseRs1), .d_UseRs2(d_UseRs2), .d_ctrl(d_ctrl), .d_rs1(d_rs1), .d_rs2(d_rs2),
    .e_MemRead(e_MemRead), .e_rd(e_rd), .e_rdnz(e_rdnz), .flush(FLUSH), .d_ctrl_q(d_ctrl_q), .pcen(pcen),
    .stall(STALL));
  ForwardUnit forwardunit_1 (
    .d_rs1(d_rs1), .d_rs2(d_rs2), .e_rd(e_rd), .e_rs1(e_rs1), .e_rs2(e_rs2), .m_RegWrite(m_RegWrite),
    .m_rd(m_rd), .w_RegWrite(w_RegWrite), .w_rd(w_rd), .e_rdnz(e_rdnz), .fm1(fm1), .fm2(fm2), .fw1(fw1),
    .fw2(fw2), .wb_byp1(wb_byp1), .wb_byp2(wb_byp2));
  RegFile regfile_1 (
    .clk(clk), .we(w_RegWrite), .rs1(d_rs1), .rs2(d_rs2), .rd(w_rd), .wd(w_data), .r1(regfile_1_r1),
    .r2(regfile_1_r2));
  ImmGen immgen_1 (.instr(d_instr), .sel(maincontrol_1_d_immsel), .imm(d_imm));
  Multiplexer #(.width(32), .select(1)) multiplexer_3 (
    .in0(regfile_1_r1), .in1(w_data), .out(multiplexer_3_out), .sel(wb_byp1));
  Multiplexer #(.width(32), .select(1)) multiplexer_4 (
    .in0(regfile_1_r2), .in1(w_data), .out(multiplexer_4_out), .sel(wb_byp2));
  ID_EX id_ex_1 (
    .clk(clk), .d_ctrl_q(d_ctrl_q), .d_f3(d_f3), .d_imm(d_imm), .d_pc(d_pc), .d_r1(multiplexer_3_out),
    .d_r2(multiplexer_4_out), .d_rd(d_rd), .d_rs1(d_rs1), .d_rs2(d_rs2), .e_ALUOp(e_ALUOp), .e_ASel(e_ASel),
    .e_BSel(e_BSel), .e_Branch(e_Branch), .e_Jal(e_Jal), .e_Jalr(e_Jalr), .e_MemRead(e_MemRead),
    .e_ResPC4(e_ResPC4), .e_ctrl(e_ctrl), .e_f3(e_f3), .e_imm(e_imm), .e_pc(e_pc), .e_r1(id_ex_1_e_r1),
    .e_r2(id_ex_1_e_r2), .e_rd(e_rd), .e_rs1(e_rs1), .e_rs2(e_rs2));
  Multiplexer #(.width(32), .select(1)) multiplexer_5 (
    .in0(id_ex_1_e_r1), .in1(w_data), .out(multiplexer_5_out), .sel(fw1));
  Multiplexer #(.width(32), .select(1)) multiplexer_6 (
    .in0(id_ex_1_e_r2), .in1(w_data), .out(multiplexer_6_out), .sel(fw2));
  Multiplexer #(.width(32), .select(1)) multiplexer_7 (
    .in0(multiplexer_5_out), .in1({m_res, m_boff}), .out(multiplexer_7_out), .sel(fm1));
  Multiplexer #(.width(32), .select(1)) multiplexer_8 (
    .in0(multiplexer_6_out), .in1({m_res, m_boff}), .out(fb), .sel(fm2));
  Multiplexer #(.width(32), .select(2)) multiplexer_9 (
    .in0(multiplexer_7_out), .in1(e_pc), .in2({32{1'b0}}), .out(multiplexer_9_out), .sel(e_ASel));  // open: in3
  Multiplexer #(.width(32), .select(1)) multiplexer_10 (.in0(fb), .in1(e_imm), .out(multiplexer_10_out), .sel(e_BSel));
  Adder #(.width(32)) adder_2 (.a(e_pc), .b(e_imm), .out(e_brt));  // open: cin, cout
  Adder #(.width(32)) adder_3 (.a(e_pc), .b(32'h4), .out(e_pc4));  // open: cin, cout
  BranchUnit branchunit_1 (.a(multiplexer_7_out), .b(fb), .f3(e_f3), .cond(branchunit_1_cond));
  ALU alu_1 (.a(multiplexer_9_out), .b(multiplexer_10_out), .op(e_ALUOp), .y(alu_1_y));
  and and_1 (and_1_out, e_Branch, branchunit_1_cond);
  assign e_jalrt = alu_1_y & 32'hfffffffe;  // AND_Gate and_2, 32 bits wide
  Multiplexer #(.width(32), .select(1)) multiplexer_11 (
    .in0(alu_1_y), .in1(e_pc4), .out(multiplexer_11_out), .sel(e_ResPC4));
  or or_1 (FLUSH, and_1_out, e_Jal, e_Jalr);
  Multiplexer #(.width(32), .select(1)) multiplexer_12 (.in0(e_brt), .in1(e_jalrt), .out(e_target), .sel(e_Jalr));
  EX_MEM ex_mem_1 (
    .clk(clk), .e_ctrl(e_ctrl), .e_f3(e_f3), .e_rd(e_rd), .e_res(multiplexer_11_out), .fb(fb),
    .m_MemWrite(m_MemWrite), .m_RegWrite(m_RegWrite), .m_ctrl(m_ctrl), .m_f3(m_f3), .m_r2(ex_mem_1_m_r2),
    .m_rd(m_rd), .m_res({m_res, m_boff}));
  StoreUnit storeunit_1 (.old(m_mraw), .wd(ex_mem_1_m_r2), .off(m_boff), .f3(m_f3), .\new (storeunit_1_new));
  RAM #(.addrWidth(10), .dataWidth(32), .asyncread("true")) DMEM (
    .addr(m_res[11:2]), .we(m_MemWrite), .oe(1'b1), .clk(clk), .din(storeunit_1_new), .dout(m_mraw));
  LoadUnit loadunit_1 (.din(m_mraw), .off(m_boff), .f3(m_f3), .v(loadunit_1_v));
  MEM_WB mem_wb_1 (
    .clk(clk), .m_ctrl(m_ctrl), .m_mdata(loadunit_1_v), .m_rd(m_rd), .m_res({m_res, m_boff}), .w_Halt(halt),
    .w_MemRead(w_MemRead), .w_RegWrite(w_RegWrite), .w_mdata(w_mdata), .w_rd(w_rd), .w_res(mem_wb_1_w_res));
  Multiplexer #(.width(32), .select(1)) multiplexer_13 (
    .in0(mem_wb_1_w_res), .in1(w_mdata), .out(w_data), .sel(w_MemRead));

  // Other names for the same wires on the sheet: m_res[1:0] = m_boff; pc[31:0] = PC_out; w_Halt = halt

  // Notes on the sheet:
  //   PC next
  //   IF
  //   contents of IMEM (hex, n*v repeats v):
  //   73
  //   IMEM
  //   IF/ID
  //   ID
  //   ID/EX
  //   EX
  //   EX/MEM
  //   MEM (DMEM)
  //   MEM/WB
  //   WB
endmodule

module ALU (
  input  [31:0] a,
  input  [31:0] b,
  input  [3:0] op,
  output [31:0] y
);

  wire comparator_1_lt, comparator_2_lt;
  wire [31:0] add, \and , bit_extender_1_out, bit_extender_2_out, \or , shifter_1_out, shifter_2_out,
       shifter_3_out, sub, \xor ;

  Adder #(.width(32)) adder_1 (.a(a), .b(b), .out(add));  // open: cin, cout
  Subtractor #(.width(32)) subtractor_1 (.a(a), .b(b), .out(sub));  // open: bin, bout
  Comparator #(.width(32), .mode("twosComplement")) comparator_1 (.a(a), .b(b), .lt(comparator_1_lt));  // open: gt, eq
  Comparator #(.width(32), .mode("unsigned")) comparator_2 (.a(a), .b(b), .lt(comparator_2_lt));  // open: gt, eq
  assign \xor  = a ^ b;  // XOR_Gate xor_1, 32 bits wide
  assign \or  = a | b;  // OR_Gate or_1, 32 bits wide
  assign \and  = a & b;  // AND_Gate and_1, 32 bits wide
  Shifter #(.width(32), .shift("ll")) shifter_1 (.in(a), .\dist (b[4:0]), .out(shifter_1_out));
  Shifter #(.width(32), .shift("lr")) shifter_2 (.in(a), .\dist (b[4:0]), .out(shifter_2_out));
  Shifter #(.width(32), .shift("ar")) shifter_3 (.in(a), .\dist (b[4:0]), .out(shifter_3_out));
  assign bit_extender_1_out = {{31{1'b0}}, comparator_1_lt};  // Bit_Extender bit_extender_1
  assign bit_extender_2_out = {{31{1'b0}}, comparator_2_lt};  // Bit_Extender bit_extender_2
  Multiplexer #(.width(32), .select(4)) multiplexer_1 (
    .in0(add), .in1(sub), .in2(shifter_1_out), .in3(bit_extender_1_out), .in4(bit_extender_2_out),
    .in5(\xor ), .in6(shifter_2_out), .in7(shifter_3_out), .in8(\or ), .in9(\and ), .in10({32{1'b0}}),
    .in11({32{1'b0}}), .in12({32{1'b0}}), .in13({32{1'b0}}), .in14({32{1'b0}}), .in15({32{1'b0}}), .out(y),
    .sel(op));
endmodule

module RegFile (
  input  clk,
  input  we,
  input  [4:0] rs1,
  input  [4:0] rs2,
  input  [4:0] rd,
  input  [31:0] wd,
  output [31:0] r1,
  output [31:0] r2
);

  wire and_1_out, and_2_out, and_3_out, and_4_out, and_5_out, and_6_out, and_7_out, and_8_out, and_9_out,
       and_10_out, and_11_out, and_12_out, and_13_out, and_14_out, and_15_out, and_16_out, and_17_out,
       and_18_out, and_19_out, and_20_out, and_21_out, and_22_out, and_23_out, and_24_out, and_25_out,
       and_26_out, and_27_out, and_28_out, and_29_out, and_30_out, and_31_out, dec1, dec2, dec3, dec4, dec12,
       dec20, dec28, decoder_1_out5, decoder_1_out6, decoder_1_out7, decoder_1_out8, decoder_1_out9,
       decoder_1_out10, decoder_1_out11, decoder_1_out13, decoder_1_out14, decoder_1_out15, decoder_1_out16,
       decoder_1_out17, decoder_1_out18, decoder_1_out19, decoder_1_out21, decoder_1_out22, decoder_1_out23,
       decoder_1_out24, decoder_1_out25, decoder_1_out26, decoder_1_out27, decoder_1_out29, decoder_1_out30,
       decoder_1_out31;
  wire [31:0] register_4_q, register_7_q, register_8_q, register_9_q, register_11_q, register_12_q,
       register_13_q, register_15_q, register_16_q, register_17_q, register_18_q, register_19_q,
       register_20_q, register_21_q, register_23_q, register_24_q, register_25_q, register_27_q,
       register_28_q, register_29_q, register_30_q, register_31_q, x1, x2, x3, x5, x6, x10, x14, x22, x26;

  Decoder #(.select(5), .enable("false")) decoder_1 (
    .out1(dec1), .out2(dec2), .out3(dec3), .out4(dec4), .out5(decoder_1_out5), .out6(decoder_1_out6),
    .out7(decoder_1_out7), .out8(decoder_1_out8), .out9(decoder_1_out9), .out10(decoder_1_out10),
    .out11(decoder_1_out11), .out12(dec12), .out13(decoder_1_out13), .out14(decoder_1_out14),
    .out15(decoder_1_out15), .out16(decoder_1_out16), .out17(decoder_1_out17), .out18(decoder_1_out18),
    .out19(decoder_1_out19), .out20(dec20), .out21(decoder_1_out21), .out22(decoder_1_out22),
    .out23(decoder_1_out23), .out24(decoder_1_out24), .out25(decoder_1_out25), .out26(decoder_1_out26),
    .out27(decoder_1_out27), .out28(dec28), .out29(decoder_1_out29), .out30(decoder_1_out30),
    .out31(decoder_1_out31), .sel(rd));  // open: out0
  and and_1 (and_1_out, we, dec1);
  and and_2 (and_2_out, we, dec2);
  and and_3 (and_3_out, we, dec3);
  and and_4 (and_4_out, we, dec4);
  and and_5 (and_5_out, we, decoder_1_out5);
  and and_6 (and_6_out, we, decoder_1_out6);
  and and_7 (and_7_out, we, decoder_1_out7);
  and and_8 (and_8_out, we, decoder_1_out8);
  and and_9 (and_9_out, we, decoder_1_out9);
  and and_10 (and_10_out, we, decoder_1_out10);
  and and_11 (and_11_out, we, decoder_1_out11);
  and and_12 (and_12_out, we, dec12);
  and and_13 (and_13_out, we, decoder_1_out13);
  and and_14 (and_14_out, we, decoder_1_out14);
  and and_15 (and_15_out, we, decoder_1_out15);
  and and_16 (and_16_out, we, decoder_1_out16);
  and and_17 (and_17_out, we, decoder_1_out17);
  and and_18 (and_18_out, we, decoder_1_out18);
  and and_19 (and_19_out, we, decoder_1_out19);
  and and_20 (and_20_out, we, dec20);
  and and_21 (and_21_out, we, decoder_1_out21);
  and and_22 (and_22_out, we, decoder_1_out22);
  and and_23 (and_23_out, we, decoder_1_out23);
  and and_24 (and_24_out, we, decoder_1_out24);
  and and_25 (and_25_out, we, decoder_1_out25);
  and and_26 (and_26_out, we, decoder_1_out26);
  and and_27 (and_27_out, we, decoder_1_out27);
  and and_28 (and_28_out, we, dec28);
  and and_29 (and_29_out, we, decoder_1_out29);
  and and_30 (and_30_out, we, decoder_1_out30);
  and and_31 (and_31_out, we, decoder_1_out31);
  Register #(.width(32)) register_1 (.D(wd), .en(and_1_out), .clk(clk), .Q(x1));  // open: clr
  Register #(.width(32)) register_2 (.D(wd), .en(and_2_out), .clk(clk), .Q(x2));  // open: clr
  Register #(.width(32)) register_3 (.D(wd), .en(and_3_out), .clk(clk), .Q(x3));  // open: clr
  Register #(.width(32)) register_4 (.D(wd), .en(and_4_out), .clk(clk), .Q(register_4_q));  // open: clr
  Register #(.width(32)) register_5 (.D(wd), .en(and_5_out), .clk(clk), .Q(x5));  // open: clr
  Register #(.width(32)) register_6 (.D(wd), .en(and_6_out), .clk(clk), .Q(x6));  // open: clr
  Register #(.width(32)) register_7 (.D(wd), .en(and_7_out), .clk(clk), .Q(register_7_q));  // open: clr
  Register #(.width(32)) register_8 (.D(wd), .en(and_8_out), .clk(clk), .Q(register_8_q));  // open: clr
  Register #(.width(32)) register_9 (.D(wd), .en(and_9_out), .clk(clk), .Q(register_9_q));  // open: clr
  Register #(.width(32)) register_10 (.D(wd), .en(and_10_out), .clk(clk), .Q(x10));  // open: clr
  Register #(.width(32)) register_11 (.D(wd), .en(and_11_out), .clk(clk), .Q(register_11_q));  // open: clr
  Register #(.width(32)) register_12 (.D(wd), .en(and_12_out), .clk(clk), .Q(register_12_q));  // open: clr
  Register #(.width(32)) register_13 (.D(wd), .en(and_13_out), .clk(clk), .Q(register_13_q));  // open: clr
  Register #(.width(32)) register_14 (.D(wd), .en(and_14_out), .clk(clk), .Q(x14));  // open: clr
  Register #(.width(32)) register_15 (.D(wd), .en(and_15_out), .clk(clk), .Q(register_15_q));  // open: clr
  Register #(.width(32)) register_16 (.D(wd), .en(and_16_out), .clk(clk), .Q(register_16_q));  // open: clr
  Register #(.width(32)) register_17 (.D(wd), .en(and_17_out), .clk(clk), .Q(register_17_q));  // open: clr
  Register #(.width(32)) register_18 (.D(wd), .en(and_18_out), .clk(clk), .Q(register_18_q));  // open: clr
  Register #(.width(32)) register_19 (.D(wd), .en(and_19_out), .clk(clk), .Q(register_19_q));  // open: clr
  Register #(.width(32)) register_20 (.D(wd), .en(and_20_out), .clk(clk), .Q(register_20_q));  // open: clr
  Register #(.width(32)) register_21 (.D(wd), .en(and_21_out), .clk(clk), .Q(register_21_q));  // open: clr
  Register #(.width(32)) register_22 (.D(wd), .en(and_22_out), .clk(clk), .Q(x22));  // open: clr
  Register #(.width(32)) register_23 (.D(wd), .en(and_23_out), .clk(clk), .Q(register_23_q));  // open: clr
  Register #(.width(32)) register_24 (.D(wd), .en(and_24_out), .clk(clk), .Q(register_24_q));  // open: clr
  Register #(.width(32)) register_25 (.D(wd), .en(and_25_out), .clk(clk), .Q(register_25_q));  // open: clr
  Register #(.width(32)) register_26 (.D(wd), .en(and_26_out), .clk(clk), .Q(x26));  // open: clr
  Register #(.width(32)) register_27 (.D(wd), .en(and_27_out), .clk(clk), .Q(register_27_q));  // open: clr
  Register #(.width(32)) register_28 (.D(wd), .en(and_28_out), .clk(clk), .Q(register_28_q));  // open: clr
  Register #(.width(32)) register_29 (.D(wd), .en(and_29_out), .clk(clk), .Q(register_29_q));  // open: clr
  Register #(.width(32)) register_30 (.D(wd), .en(and_30_out), .clk(clk), .Q(register_30_q));  // open: clr
  Register #(.width(32)) register_31 (.D(wd), .en(and_31_out), .clk(clk), .Q(register_31_q));  // open: clr
  Multiplexer #(.width(32), .select(5)) multiplexer_1 (
    .in0({32{1'b0}}), .in1(x1), .in2(x2), .in3(x3), .in4(register_4_q), .in5(x5), .in6(x6),
    .in7(register_7_q), .in8(register_8_q), .in9(register_9_q), .in10(x10), .in11(register_11_q),
    .in12(register_12_q), .in13(register_13_q), .in14(x14), .in15(register_15_q), .in16(register_16_q),
    .in17(register_17_q), .in18(register_18_q), .in19(register_19_q), .in20(register_20_q),
    .in21(register_21_q), .in22(x22), .in23(register_23_q), .in24(register_24_q), .in25(register_25_q),
    .in26(x26), .in27(register_27_q), .in28(register_28_q), .in29(register_29_q), .in30(register_30_q),
    .in31(register_31_q), .out(r1), .sel(rs1));
  Multiplexer #(.width(32), .select(5)) multiplexer_2 (
    .in0({32{1'b0}}), .in1(x1), .in2(x2), .in3(x3), .in4(register_4_q), .in5(x5), .in6(x6),
    .in7(register_7_q), .in8(register_8_q), .in9(register_9_q), .in10(x10), .in11(register_11_q),
    .in12(register_12_q), .in13(register_13_q), .in14(x14), .in15(register_15_q), .in16(register_16_q),
    .in17(register_17_q), .in18(register_18_q), .in19(register_19_q), .in20(register_20_q),
    .in21(register_21_q), .in22(x22), .in23(register_23_q), .in24(register_24_q), .in25(register_25_q),
    .in26(x26), .in27(register_27_q), .in28(register_28_q), .in29(register_29_q), .in30(register_30_q),
    .in31(register_31_q), .out(r2), .sel(rs2));
endmodule

module ImmGen (
  input  [31:0] instr,
  input  [2:0] sel,
  output [31:0] imm
);

  wire [31:0] bit_extender_2_out, bit_extender_3_out, bit_extender_4_out, immI;

  assign immI = {{20{instr[31]}}, instr[31:20]};  // Bit_Extender bit_extender_1
  assign bit_extender_2_out = {{20{instr[31]}}, {instr[31:25], instr[11:7]}};  // Bit_Extender bit_extender_2
  assign bit_extender_3_out = {{19{instr[31]}}, {instr[31], instr[7], instr[30:25], instr[11:8], 1'b0}};  // Bit_Extender bit_extender_3
  assign bit_extender_4_out = {{11{instr[31]}}, {instr[31], instr[19:12], instr[20], instr[30:21], 1'b0}};  // Bit_Extender bit_extender_4
  Multiplexer #(.width(32), .select(3)) multiplexer_1 (
    .in0(immI), .in1(bit_extender_2_out), .in2(bit_extender_3_out), .in3({instr[31:12], {12{1'b0}}}),
    .in4(bit_extender_4_out), .in5({32{1'b0}}), .in6({32{1'b0}}), .in7({32{1'b0}}), .out(imm), .sel(sel));

  // Other names for the same wires on the sheet: b4_1[3:0] = instr[11:8];
  //   b13[12:1] = {instr[31], instr[7], instr[30:25], instr[11:8]}; s12[11:0] = {instr[31:25], instr[11:7]};
  //   s_lo[4:0] = instr[11:7]; b11 = instr[7]; immU[31:12] = instr[31:12]; j10_1[9:0] = instr[30:21];
  //   j21[20:1] = {instr[31], instr[19:12], instr[20], instr[30:21]}; u20[19:0] = instr[31:12];
  //   b10_5[5:0] = instr[30:25]; s_hi[6:0] = instr[31:25]; j11 = instr[20]; j19_12[7:0] = instr[19:12];
  //   b12 = instr[31]
endmodule

module BranchUnit (
  input  [31:0] a,
  input  [31:0] b,
  input  [2:0] f3,
  output cond
);

  wire eq, lts, ltu, not_1_out, not_2_out, not_3_out;

  Comparator #(.width(32), .mode("twosComplement")) comparator_1 (.a(a), .b(b), .eq(eq), .lt(lts));  // open: gt
  Comparator #(.width(32), .mode("unsigned")) comparator_2 (.a(a), .b(b), .lt(ltu));  // open: gt, eq
  not not_1 (not_1_out, eq);
  not not_2 (not_2_out, lts);
  not not_3 (not_3_out, ltu);
  Multiplexer #(.width(1), .select(3)) multiplexer_1 (
    .in0(eq), .in1(not_1_out), .in2(1'b0), .in3(1'b0), .in4(lts), .in5(not_2_out), .in6(ltu),
    .in7(not_3_out), .out(cond), .sel(f3));
endmodule

module Control (
  input  [31:0] instr,
  output [19:0] ctrl
);

  ROM #(.addrWidth(9), .dataWidth(20)) u_CTRL (.addr({instr[30], instr[14:12], instr[6:2]}), .data(ctrl));

  // Other names for the same wires on the sheet: caddr[8:0] = {instr[30], instr[14:12], instr[6:2]};
  //   op5[4:0] = instr[6:2]; f3[2:0] = instr[14:12]; f7b = instr[30]

  // Notes on the sheet:
  //   contents of CTRL (hex, n*v repeats v):
  //   40109 0 0 0 40009 180b 0 0 c0a08 0 0 0 c0001 180d 0 0 0 0 0 0 0 0 0 0 c5000 50409 0 a401 20000 0 0 0
  //   40109 0 0 0 40029 180b 0 0 c0a08 0 0 0 c0021 180d 0 0 0 0 0 0 0 0 0 0 c5000 0 0 a401 20000 0 0 0
  //   40109 0 0 0 40039 180b 0 0 c0a08 0 0 0 c0031 180d 0 0 0 0 0 0 0 0 0 0 0 0 0 a401 20000 0 0 0 0 0 0 0
  //   40049 180b 0 0 0 0 0 0 c0041 180d 0 0 0 0 0 0 0 0 0 0 0 0 0 a401 20000 0 0 0 40109 0 0 0 40059 180b
  //   0 0 0 0 0 0 c0051 180d 0 0 0 0 0 0 0 0 0 0 c5000 0 0 a401 20000 0 0 0 40109 0 0 0 40069 180b 0 0 0 0
  //   0 0 c0061 180d 0 0 0 0 0 0 0 0 0 0 c5000 0 0 a401 20000 0 0 0 0 0 0 0 40089 180b 0 0 0 0 0 0 c0081
  //   180d 0 0 0 0 0 0 0 0 0 0 c5000 0 0 a401 20000 0 0 0 0 0 0 0 40099 180b 0 0 0 0 0 0 c0091 180d 0 0 0
  //   0 0 0 0 0 0 0 c5000 0 0 a401 20000 0 0 0 40109 0 0 0 40009 180b 0 0 c0a08 0 0 0 c0011 180d 0 0 0 0 0
  //   0 0 0 0 0 c5000 50409 0 a401 20000 0 0 0 40109 0 0 0 40029 180b 0 0 c0a08 0 0 0 0 180d 0 0 0 0 0 0 0
  //   0 0 0 c5000 0 0 a401 20000 0 0 0 40109 0 0 0 40039 180b 0 0 c0a08 0 0 0 0 180d 0 0 0 0 0 0 0 0 0 0 0
  //   0 0 a401 20000 0 0 0 0 0 0 0 40049 180b 0 0 0 0 0 0 0 180d 0 0 0 0 0 0 0 0 0 0 0 0 0 a401 20000 0 0
  //   0 40109 0 0 0 40059 180b 0 0 0 0 0 0 0 180d 0 0 0 0 0 0 0 0 0 0 c5000 0 0 a401 20000 0 0 0 40109 0 0
  //   0 40079 180b 0 0 0 0 0 0 c0071 180d 0 0 0 0 0 0 0 0 0 0 c5000 0 0 a401 20000 0 0 0 0 0 0 0 40089
  //   180b 0 0 0 0 0 0 0 180d 0 0 0 0 0 0 0 0 0 0 c5000 0 0 a401 20000 0 0 0 0 0 0 0 40099 180b 0 0 0 0 0
  //   0 0 180d 0 0 0 0 0 0 0 0 0 0 c5000 0 0 a401 20000 0 0 0
endmodule

module LoadUnit (
  input  [31:0] din,
  input  [1:0] off,
  input  [2:0] f3,
  output [31:0] v
);

  wire [31:0] bit_extender_2_out, bit_extender_4_out, sb, sh16, x;

  Shifter #(.width(32), .shift("lr")) shifter_1 (.in(din), .\dist ({off, 3'b000}), .out(x));
  assign sb = {{24{x[7]}}, x[7:0]};  // Bit_Extender bit_extender_1
  assign bit_extender_2_out = {{24{1'b0}}, x[7:0]};  // Bit_Extender bit_extender_2
  assign sh16 = {{16{x[15]}}, x[15:0]};  // Bit_Extender bit_extender_3
  assign bit_extender_4_out = {{16{1'b0}}, x[15:0]};  // Bit_Extender bit_extender_4
  Multiplexer #(.width(32), .select(3)) multiplexer_1 (
    .in0(sb), .in1(sh16), .in2(x), .in3(x), .in4(bit_extender_2_out), .in5(bit_extender_4_out), .in6(x),
    .in7(x), .out(v), .sel(f3));

  // Other names for the same wires on the sheet: sh[4:3] = off
endmodule

module StoreUnit (
  input  [31:0] old,
  input  [31:0] wd,
  input  [1:0] off,
  input  [2:0] f3,
  output [31:0] \new 
);

  wire [31:0] and_2_out, ins, multiplexer_1_out, not_1_out, shifter_2_out, wds;

  Multiplexer #(.width(32), .select(2)) multiplexer_1 (
    .in0(32'hff), .in1(32'hffff), .in2({32{1'b1}}), .in3({32{1'b1}}), .out(multiplexer_1_out), .sel(f3[1:0]));
  Shifter #(.width(32), .shift("ll")) shifter_1 (.in(wd), .\dist ({off, 3'b000}), .out(wds));
  Shifter #(.width(32), .shift("ll")) shifter_2 (.in(multiplexer_1_out), .\dist ({off, 3'b000}), .out(shifter_2_out));
  assign not_1_out = ~shifter_2_out;  // NOT_Gate not_1, 32 bits wide
  assign ins = wds & shifter_2_out;  // AND_Gate and_1, 32 bits wide
  assign and_2_out = old & not_1_out;  // AND_Gate and_2, 32 bits wide
  assign \new  = and_2_out | ins;  // OR_Gate or_1, 32 bits wide

  // Other names for the same wires on the sheet: sz[1:0] = f3[1:0]; sh[4:3] = off
endmodule

module IF_ID (
  input  clk,
  input  [31:0] f_instr_q,
  input  [31:0] pc,
  input  pcen,
  output [31:0] d_instr,
  output [31:0] d_pc
);

  Register #(.width(32)) register_1 (.D(pc), .en(pcen), .clk(clk), .Q(d_pc));  // open: clr
  Register #(.width(32)) register_2 (.D(f_instr_q), .en(pcen), .clk(clk), .Q(d_instr));  // open: clr
endmodule

module InstrDecode (
  input  [31:0] d_instr,
  output [2:0] d_f3,
  output [4:0] d_rd,
  output [4:0] d_rs1,
  output [4:0] d_rs2
);


  assign d_f3 = d_instr[14:12];
  assign d_rd = d_instr[11:7];
  assign d_rs1 = d_instr[19:15];
  assign d_rs2 = d_instr[24:20];
endmodule

module MainControl (
  input  [31:0] d_instr,
  output [2:0] d_ImmSel,
  output d_UseRs1,
  output d_UseRs2,
  output [19:0] d_ctrl
);

  Control control_1 (.instr(d_instr), .ctrl(d_ctrl));

  assign d_ImmSel = d_ctrl[13:11];
  assign d_UseRs1 = d_ctrl[18];
  assign d_UseRs2 = d_ctrl[19];
endmodule

module HazardUnit (
  input  d_UseRs1,
  input  d_UseRs2,
  input  [19:0] d_ctrl,
  input  [4:0] d_rs1,
  input  [4:0] d_rs2,
  input  e_MemRead,
  input  [4:0] e_rd,
  input  e_rdnz,
  input  flush,
  output [19:0] d_ctrl_q,
  output pcen,
  output stall
);

  wire and_1_out, and_2_out, bubble, comparator_1_eq, comparator_2_eq, not_1_out, or_1_out;

  Comparator #(.width(5), .mode("unsigned")) comparator_1 (.a(e_rd), .b(d_rs1), .eq(comparator_1_eq));  // open: gt, lt
  Comparator #(.width(5), .mode("unsigned")) comparator_2 (.a(e_rd), .b(d_rs2), .eq(comparator_2_eq));  // open: gt, lt
  and and_1 (and_1_out, comparator_1_eq, d_UseRs1);
  and and_2 (and_2_out, comparator_2_eq, d_UseRs2);
  or or_1 (or_1_out, and_1_out, and_2_out);
  and and_3 (stall, e_MemRead, e_rdnz, or_1_out);
  or or_2 (bubble, stall, flush);
  not not_1 (not_1_out, stall);
  Multiplexer #(.width(20), .select(1)) multiplexer_1 (.in0(d_ctrl), .in1({20{1'b0}}), .out(d_ctrl_q), .sel(bubble));
  or or_3 (pcen, not_1_out, flush);
endmodule

module ForwardUnit (
  input  [4:0] d_rs1,
  input  [4:0] d_rs2,
  input  [4:0] e_rd,
  input  [4:0] e_rs1,
  input  [4:0] e_rs2,
  input  m_RegWrite,
  input  [4:0] m_rd,
  input  w_RegWrite,
  input  [4:0] w_rd,
  output e_rdnz,
  output fm1,
  output fm2,
  output fw1,
  output fw2,
  output wb_byp1,
  output wb_byp2
);

  wire comparator_1_eq, comparator_2_eq, comparator_3_eq, fm_eq1, fm_eq2, fw_eq1, fw_eq2, not_1_out,
       not_2_out, wb_eq1, wb_eq2;

  Comparator #(.width(5), .mode("unsigned")) comparator_1 (
    .a(w_rd), .b({5{1'b0}}), .eq(comparator_1_eq));  // open: gt, lt
  Comparator #(.width(5), .mode("unsigned")) comparator_2 (
    .a(m_rd), .b({5{1'b0}}), .eq(comparator_2_eq));  // open: gt, lt
  Comparator #(.width(5), .mode("unsigned")) comparator_3 (
    .a(e_rd), .b({5{1'b0}}), .eq(comparator_3_eq));  // open: gt, lt
  Comparator #(.width(5), .mode("unsigned")) comparator_4 (.a(w_rd), .b(d_rs1), .eq(wb_eq1));  // open: gt, lt
  Comparator #(.width(5), .mode("unsigned")) comparator_5 (.a(m_rd), .b(e_rs1), .eq(fm_eq1));  // open: gt, lt
  Comparator #(.width(5), .mode("unsigned")) comparator_6 (.a(w_rd), .b(e_rs1), .eq(fw_eq1));  // open: gt, lt
  Comparator #(.width(5), .mode("unsigned")) comparator_7 (.a(w_rd), .b(d_rs2), .eq(wb_eq2));  // open: gt, lt
  Comparator #(.width(5), .mode("unsigned")) comparator_8 (.a(m_rd), .b(e_rs2), .eq(fm_eq2));  // open: gt, lt
  Comparator #(.width(5), .mode("unsigned")) comparator_9 (.a(w_rd), .b(e_rs2), .eq(fw_eq2));  // open: gt, lt
  not not_1 (not_1_out, comparator_1_eq);
  not not_2 (not_2_out, comparator_2_eq);
  not not_3 (e_rdnz, comparator_3_eq);
  and and_1 (wb_byp1, wb_eq1, w_RegWrite, not_1_out);
  and and_2 (fm1, fm_eq1, m_RegWrite, not_2_out);
  and and_3 (fw1, fw_eq1, w_RegWrite, not_1_out);
  and and_4 (wb_byp2, wb_eq2, w_RegWrite, not_1_out);
  and and_5 (fm2, fm_eq2, m_RegWrite, not_2_out);
  and and_6 (fw2, fw_eq2, w_RegWrite, not_1_out);
endmodule

module ID_EX (
  input  clk,
  input  [19:0] d_ctrl_q,
  input  [2:0] d_f3,
  input  [31:0] d_imm,
  input  [31:0] d_pc,
  input  [31:0] d_r1,
  input  [31:0] d_r2,
  input  [4:0] d_rd,
  input  [4:0] d_rs1,
  input  [4:0] d_rs2,
  output [3:0] e_ALUOp,
  output [1:0] e_ASel,
  output e_BSel,
  output e_Branch,
  output e_Jal,
  output e_Jalr,
  output e_MemRead,
  output e_ResPC4,
  output [19:0] e_ctrl,
  output [2:0] e_f3,
  output [31:0] e_imm,
  output [31:0] e_pc,
  output [31:0] e_r1,
  output [31:0] e_r2,
  output [4:0] e_rd,
  output [4:0] e_rs1,
  output [4:0] e_rs2
);

  Register #(.width(20)) register_1 (
    .D(d_ctrl_q), .clk(clk), .Q({e_ctrl[19:15], e_Branch, e_ctrl[13:8], e_ALUOp, e_BSel, e_ASel, e_ctrl[0]}));  // open: en, clr
  Register #(.width(32)) register_2 (.D(d_pc), .clk(clk), .Q(e_pc));  // open: en, clr
  Register #(.width(32)) register_3 (.D(d_r1), .clk(clk), .Q(e_r1));  // open: en, clr
  Register #(.width(32)) register_4 (.D(d_r2), .clk(clk), .Q(e_r2));  // open: en, clr
  Register #(.width(32)) register_5 (.D(d_imm), .clk(clk), .Q(e_imm));  // open: en, clr
  Register #(.width(5)) register_6 (.D(d_rs1), .clk(clk), .Q(e_rs1));  // open: en, clr
  Register #(.width(5)) register_7 (.D(d_rs2), .clk(clk), .Q(e_rs2));  // open: en, clr
  Register #(.width(5)) register_8 (.D(d_rd), .clk(clk), .Q(e_rd));  // open: en, clr
  Register #(.width(3)) register_9 (.D(d_f3), .clk(clk), .Q(e_f3));  // open: en, clr

  assign {e_ctrl[14], e_ctrl[7:1]} = {e_Branch, e_ALUOp, e_BSel, e_ASel};
  assign e_Jal = e_ctrl[15];
  assign e_Jalr = e_ctrl[16];
  assign e_MemRead = e_ctrl[8];
  assign e_ResPC4 = e_ctrl[10];
endmodule

module EX_MEM (
  input  clk,
  input  [19:0] e_ctrl,
  input  [2:0] e_f3,
  input  [4:0] e_rd,
  input  [31:0] e_res,
  input  [31:0] fb,
  output m_MemWrite,
  output m_RegWrite,
  output [19:0] m_ctrl,
  output [2:0] m_f3,
  output [31:0] m_r2,
  output [4:0] m_rd,
  output [31:0] m_res
);

  Register #(.width(20)) register_1 (.D(e_ctrl), .clk(clk), .Q(m_ctrl));  // open: en, clr
  Register #(.width(32)) register_2 (.D(e_res), .clk(clk), .Q(m_res));  // open: en, clr
  Register #(.width(32)) register_3 (.D(fb), .clk(clk), .Q(m_r2));  // open: en, clr
  Register #(.width(5)) register_4 (.D(e_rd), .clk(clk), .Q(m_rd));  // open: en, clr
  Register #(.width(3)) register_5 (.D(e_f3), .clk(clk), .Q(m_f3));  // open: en, clr

  assign m_MemWrite = m_ctrl[9];
  assign m_RegWrite = m_ctrl[0];
endmodule

module MEM_WB (
  input  clk,
  input  [19:0] m_ctrl,
  input  [31:0] m_mdata,
  input  [4:0] m_rd,
  input  [31:0] m_res,
  output w_Halt,
  output w_MemRead,
  output w_RegWrite,
  output [31:0] w_mdata,
  output [4:0] w_rd,
  output [31:0] w_res
);

  wire [19:1] w_ctrl;

  Register #(.width(20)) register_1 (
    .D(m_ctrl), .clk(clk), .Q({w_ctrl[19:18], w_Halt, w_ctrl[16:9], w_MemRead, w_ctrl[7:1], w_RegWrite}));  // open: en, clr
  Register #(.width(32)) register_2 (.D(m_res), .clk(clk), .Q(w_res));  // open: en, clr
  Register #(.width(32)) register_3 (.D(m_mdata), .clk(clk), .Q(w_mdata));  // open: en, clr
  Register #(.width(5)) register_4 (.D(m_rd), .clk(clk), .Q(w_rd));  // open: en, clr

  // Other names for the same wires on the sheet: w_ctrl (some bits) = {w_Halt, w_MemRead, w_RegWrite}
endmodule

module CycleCounter (
  input  clk,
  output [31:0] cycles
);

  wire [31:0] adder_1_out;

  Adder #(.width(32)) adder_1 (.a(cycles), .b(32'h1), .out(adder_1_out));  // open: cin, cout
  Register #(.width(32)) register_1 (.D(adder_1_out), .clk(clk), .Q(cycles));  // open: en, clr
endmodule
