// Logisim project RiscV_Pipeline_hdl_v3.circ as structural Verilog: 27 circuits, main circuit main
module main (
  input  [7:0] SW,
  input  IRQ,
  output halt,
  output [31:0] PC_out,
  output [31:0] cycles,
  output [31:0] INSTRET,
  output STALL,
  output FLUSH,
  output MSTALL,
  output [31:0] BR_CNT,
  output [31:0] BR_MISS,
  output [31:0] DC_HIT,
  output [31:0] DC_MISS,
  output [7:0] LED
);

  wire br_ev, btb_we, c_fill, c_wr, clk, csr_we, csrfile_1_irq, d_MemWrite, d_pt_q, d_RdF, d_Rs1F, d_Rs2F,
       d_UseRs1, d_UseRs2, dc_hit_ev, dcache_1_hit, dmem_we, e_actual, e_Branch, e_BSel, e_cond, e_Csr,
       e_Jal, e_Jalr, e_MemRead, e_Mret, e_pt, e_rdnz, e_Valid, f_pt, fm1, fm2, fw1, fw2, if_id_1_d_pt,
       io_we, m_MemRead, m_MemWrite, m_RegWrite, mis_ev, mmio_1_isio, msip, mtip, multiplexer_4_out, nmstall,
       pcen, take, tx_we, w_MemRead, w_rdnz, w_RegWrite, w_Valid, wb_byp1, wb_byp2;
  wire [1:0] e_ASel, m_boff;
  wire [2:0] d_f3, e_f3, e_ResSel, m_f3, maincontrol_1_d_immsel;
  wire [3:0] e_ALUOp, e_FpOp;
  wire [4:0] e_zimm;
  wire [5:0] d_rd, d_rs1, d_rs2, e_rd, e_rs1, e_rs2, ex_mem_1_m_rs2, m_rd, w_rd;
  wire [6:0] tx_d;
  wire [11:0] e_csra;
  wire [31:0] adder_1_out, and_1_out, csrfile_1_mepc, csrfile_1_mtvec, csrfile_1_rdata, d_ctrl, d_ctrl_q,
       d_imm, d_instr, d_pc, d_ptgt, dcache_1_data, e_brt, e_ctrl, e_imm, e_pc, e_pc4, e_ptgt, e_target, e_y,
       ex_mem_1_m_r2, f_ptgt, fa, fb, fpu_1_y, id_ex_1_e_r1, id_ex_1_e_r2, IMEM_data, loadunit_1_v, m_ctrl,
       m_mraw, m_r2f, m_src, mem_wb_1_w_res, mmio_1_rdata, muldiv_1_y, multiplexer_1_out, multiplexer_3_out,
       multiplexer_5_out, multiplexer_6_out, multiplexer_7_out, multiplexer_8_out, multiplexer_11_out,
       multiplexer_12_out, multiplexer_13_out, pc_pred, redir_tgt, redirectunit_1_e_ctrl_q, regfile64_1_r1,
       regfile64_1_r2, storeunit_1_new, w_data, w_mdata;
  wire [31:2] m_res;

  PerfCounters perfcounters_1 (
    .br_ev(br_ev), .c_fill(c_fill), .clk(clk), .dc_hit_ev(dc_hit_ev), .mis_ev(mis_ev), .nmstall(nmstall),
    .w_Valid(w_Valid), .br_cnt(BR_CNT), .br_miss(BR_MISS), .cycles(cycles), .dc_hit(DC_HIT),
    .dc_miss(DC_MISS), .instret(INSTRET));
  Multiplexer #(.width(32), .select(1)) multiplexer_1 (
    .in0(pc_pred), .in1(redir_tgt), .out(multiplexer_1_out), .sel(FLUSH));
  Clock clock_1 (.out(clk));
  Register #(.width(32)) register_1 (.D(multiplexer_1_out), .en(pcen), .clk(clk), .Q(PC_out));  // open: clr
  BTB btb_1 (
    .clk(clk), .rpc(PC_out), .we(btb_we), .wpc(e_pc), .wtgt(e_target), .wtk(e_actual), .ptk(f_pt),
    .ptgt(f_ptgt));
  Adder #(.width(32)) adder_1 (.a(PC_out), .b(32'h4), .out(adder_1_out));  // open: cin, cout
  Multiplexer #(.width(32), .select(1)) multiplexer_2 (.in0(adder_1_out), .in1(f_ptgt), .out(pc_pred), .sel(f_pt));
  ROM #(.addrWidth(10), .dataWidth(32)) IMEM (.addr(PC_out[11:2]), .data(IMEM_data));
  Multiplexer #(.width(32), .select(1)) multiplexer_3 (
    .in0(IMEM_data), .in1({32{1'b0}}), .out(multiplexer_3_out), .sel(FLUSH));
  Multiplexer #(.width(1), .select(1)) multiplexer_4 (.in0(f_pt), .in1(1'b0), .out(multiplexer_4_out), .sel(FLUSH));
  IF_ID if_id_1 (
    .clk(clk), .f_instr_q(multiplexer_3_out), .f_pt_q(multiplexer_4_out), .f_ptgt(f_ptgt), .pc(PC_out),
    .pcen(pcen), .d_instr(d_instr), .d_pc(d_pc), .d_pt(if_id_1_d_pt), .d_ptgt(d_ptgt));
  InstrDecode instrdecode_1 (
    .d_RdF(d_RdF), .d_Rs1F(d_Rs1F), .d_Rs2F(d_Rs2F), .d_instr(d_instr), .d_f3(d_f3), .d_rd(d_rd),
    .d_rs1(d_rs1), .d_rs2(d_rs2));
  MainControl maincontrol_1 (
    .d_instr(d_instr), .d_ImmSel(maincontrol_1_d_immsel), .d_MemWrite(d_MemWrite), .d_RdF(d_RdF),
    .d_Rs1F(d_Rs1F), .d_Rs2F(d_Rs2F), .d_UseRs1(d_UseRs1), .d_UseRs2(d_UseRs2), .d_ctrl(d_ctrl));
  HazardUnit hazardunit_1 (
    .d_MemWrite(d_MemWrite), .d_UseRs1(d_UseRs1), .d_UseRs2(d_UseRs2), .d_ctrl(d_ctrl), .d_pt(if_id_1_d_pt),
    .d_rs1(d_rs1), .d_rs2(d_rs2), .e_MemRead(e_MemRead), .e_rd(e_rd), .e_rdnz(e_rdnz), .nmstall(nmstall),
    .redir(FLUSH), .d_ctrl_q(d_ctrl_q), .d_pt_q(d_pt_q), .pcen(pcen), .stall(STALL));
  ForwardUnit forwardunit_1 (
    .d_rs1(d_rs1), .d_rs2(d_rs2), .e_rd(e_rd), .e_rs1(e_rs1), .e_rs2(e_rs2), .m_RegWrite(m_RegWrite),
    .m_rd(m_rd), .w_RegWrite(w_RegWrite), .w_rd(w_rd), .e_rdnz(e_rdnz), .fm1(fm1), .fm2(fm2), .fw1(fw1),
    .fw2(fw2), .w_rdnz(w_rdnz), .wb_byp1(wb_byp1), .wb_byp2(wb_byp2));
  CSRUnit csrunit_1 (.e_imm(e_imm), .e_rs1(e_rs1), .e_csra(e_csra), .e_zimm(e_zimm));
  RegFile64 regfile64_1 (
    .clk(clk), .we(w_RegWrite), .rs1(d_rs1), .rs2(d_rs2), .rd(w_rd), .wd(w_data), .r1(regfile64_1_r1),
    .r2(regfile64_1_r2));
  ImmGen immgen_1 (.instr(d_instr), .sel(maincontrol_1_d_immsel), .imm(d_imm));
  Multiplexer #(.width(32), .select(1)) multiplexer_5 (
    .in0(regfile64_1_r1), .in1(w_data), .out(multiplexer_5_out), .sel(wb_byp1));
  Multiplexer #(.width(32), .select(1)) multiplexer_6 (
    .in0(regfile64_1_r2), .in1(w_data), .out(multiplexer_6_out), .sel(wb_byp2));
  ID_EX id_ex_1 (
    .clk(clk), .d_ctrl_q(d_ctrl_q), .d_f3(d_f3), .d_imm(d_imm), .d_pc(d_pc), .d_pt_q(d_pt_q),
    .d_ptgt(d_ptgt), .d_r1(multiplexer_5_out), .d_r2(multiplexer_6_out), .d_rd(d_rd), .d_rs1(d_rs1),
    .d_rs2(d_rs2), .nmstall(nmstall), .e_ALUOp(e_ALUOp), .e_ASel(e_ASel), .e_BSel(e_BSel),
    .e_Branch(e_Branch), .e_Csr(e_Csr), .e_FpOp(e_FpOp), .e_Jal(e_Jal), .e_Jalr(e_Jalr),
    .e_MemRead(e_MemRead), .e_Mret(e_Mret), .e_ResSel(e_ResSel), .e_Valid(e_Valid), .e_ctrl(e_ctrl),
    .e_f3(e_f3), .e_imm(e_imm), .e_pc(e_pc), .e_pt(e_pt), .e_ptgt(e_ptgt), .e_r1(id_ex_1_e_r1),
    .e_r2(id_ex_1_e_r2), .e_rd(e_rd), .e_rs1(e_rs1), .e_rs2(e_rs2));
  Multiplexer #(.width(32), .select(1)) multiplexer_7 (
    .in0(id_ex_1_e_r1), .in1(w_data), .out(multiplexer_7_out), .sel(fw1));
  Multiplexer #(.width(32), .select(1)) multiplexer_8 (
    .in0(id_ex_1_e_r2), .in1(w_data), .out(multiplexer_8_out), .sel(fw2));
  Multiplexer #(.width(32), .select(1)) multiplexer_9 (
    .in0(multiplexer_7_out), .in1({m_res, m_boff}), .out(fa), .sel(fm1));
  Multiplexer #(.width(32), .select(1)) multiplexer_10 (
    .in0(multiplexer_8_out), .in1({m_res, m_boff}), .out(fb), .sel(fm2));
  BranchUnit branchunit_1 (.a(fa), .b(fb), .f3(e_f3), .cond(e_cond));
  Multiplexer #(.width(32), .select(2)) multiplexer_11 (
    .in0(fa), .in1(e_pc), .in2({32{1'b0}}), .out(multiplexer_11_out), .sel(e_ASel));  // open: in3
  Multiplexer #(.width(32), .select(1)) multiplexer_12 (.in0(fb), .in1(e_imm), .out(multiplexer_12_out), .sel(e_BSel));
  Adder #(.width(32)) adder_2 (.a(e_pc), .b(32'h4), .out(e_pc4));  // open: cin, cout
  Adder #(.width(32)) adder_3 (.a(e_pc), .b(e_imm), .out(e_brt));  // open: cin, cout
  ALU alu_1 (.a(multiplexer_11_out), .b(multiplexer_12_out), .op(e_ALUOp), .y(e_y));
  MulDiv muldiv_1 (.a(fa), .b(fb), .f3(e_f3), .y(muldiv_1_y));
  FPU fpu_1 (.a(fa), .b(fb), .op(e_FpOp), .rm(e_f3), .y(fpu_1_y));
  CSRFile csrfile_1 (
    .clk(clk), .en(nmstall), .we(csr_we), .addr(e_csra), .f3(e_f3), .rs1v(fa), .zimm(e_zimm), .mret(e_Mret),
    .trap(take), .epc(e_pc), .msip(msip), .mtip(mtip), .meip(IRQ), .cycles(cycles), .rdata(csrfile_1_rdata),
    .mtvec(csrfile_1_mtvec), .mepc(csrfile_1_mepc), .irq(csrfile_1_irq));  // open: cause
  assign and_1_out = e_y & 32'hfffffffe;  // AND_Gate and_1, 32 bits wide
  Multiplexer #(.width(32), .select(3)) multiplexer_13 (
    .in0(e_y), .in1(e_pc4), .in2(muldiv_1_y), .in3(csrfile_1_rdata), .in4(fpu_1_y), .in5({32{1'b0}}),
    .in6({32{1'b0}}), .in7({32{1'b0}}), .out(multiplexer_13_out), .sel(e_ResSel));
  RedirectUnit redirectunit_1 (
    .e_Branch(e_Branch), .e_Csr(e_Csr), .e_Jal(e_Jal), .e_Jalr(e_Jalr), .e_Mret(e_Mret), .e_Valid(e_Valid),
    .e_brt(e_brt), .e_cond(e_cond), .e_ctrl(e_ctrl), .e_jalrt(and_1_out), .e_pc4(e_pc4), .e_pt(e_pt),
    .e_ptgt(e_ptgt), .irq(csrfile_1_irq), .mepc(csrfile_1_mepc), .mtvec(csrfile_1_mtvec), .nmstall(nmstall),
    .br_ev(br_ev), .btb_we(btb_we), .csr_we(csr_we), .e_actual(e_actual), .e_ctrl_q(redirectunit_1_e_ctrl_q),
    .e_target(e_target), .mis_ev(mis_ev), .redir(FLUSH), .redir_tgt(redir_tgt), .take(take));
  EX_MEM ex_mem_1 (
    .clk(clk), .e_ctrl_q(redirectunit_1_e_ctrl_q), .e_f3(e_f3), .e_rd(e_rd), .e_res(multiplexer_13_out),
    .e_rs2(e_rs2), .fb(fb), .nmstall(nmstall), .m_MemRead(m_MemRead), .m_MemWrite(m_MemWrite),
    .m_RegWrite(m_RegWrite), .m_ctrl(m_ctrl), .m_f3(m_f3), .m_r2(ex_mem_1_m_r2), .m_rd(m_rd),
    .m_res({m_res, m_boff}), .m_rs2(ex_mem_1_m_rs2));
  MemFwd memfwd_1 (
    .m_MemWrite(m_MemWrite), .m_r2(ex_mem_1_m_r2), .m_rs2(ex_mem_1_m_rs2), .w_RegWrite(w_RegWrite),
    .w_data(w_data), .w_rd(w_rd), .w_rdnz(w_rdnz), .m_r2f(m_r2f));
  StoreUnit storeunit_1 (.old(m_mraw), .wd(m_r2f), .off(m_boff), .f3(m_f3), .\new (storeunit_1_new));
  RAM #(.addrWidth(10), .dataWidth(32), .asyncread("true")) DMEM (
    .addr(m_res[11:2]), .we(dmem_we), .oe(1'b1), .clk(clk), .din(storeunit_1_new), .dout(m_mraw));
  MMIO mmio_1 (
    .clk(clk), .addr({m_res, m_boff}), .we(io_we), .wdata(m_r2f), .sw(SW), .cycles(cycles),
    .rdata(mmio_1_rdata), .isio(mmio_1_isio), .led(LED), .msip(msip), .mtip(mtip), .tx_we(tx_we), .tx_d(tx_d));
  DCache dcache_1 (
    .clk(clk), .addr(m_res[11:2]), .wr(c_wr), .wdata(storeunit_1_new), .mdata(m_mraw), .fill(c_fill),
    .hit(dcache_1_hit), .data(dcache_1_data));
  TTY #(.rows(8), .cols(32)) UART_TX (.data(tx_d), .clk(clk), .we(tx_we), .clr(1'b0));
  CacheCtrl cachectrl_1 (
    .c_data(dcache_1_data), .c_hit(dcache_1_hit), .clk(clk), .io_data(mmio_1_rdata), .isio(mmio_1_isio),
    .m_MemRead(m_MemRead), .m_MemWrite(m_MemWrite), .m_mraw(m_mraw), .c_fill(c_fill), .c_wr(c_wr),
    .dc_hit_ev(dc_hit_ev), .dmem_we(dmem_we), .io_we(io_we), .m_src(m_src), .mstall(MSTALL), .nmstall(nmstall));
  LoadUnit loadunit_1 (.din(m_src), .off(m_boff), .f3(m_f3), .v(loadunit_1_v));
  MEM_WB mem_wb_1 (
    .clk(clk), .m_ctrl(m_ctrl), .m_mdata(loadunit_1_v), .m_rd(m_rd), .m_res({m_res, m_boff}),
    .nmstall(nmstall), .w_Halt(halt), .w_MemRead(w_MemRead), .w_RegWrite(w_RegWrite), .w_Valid(w_Valid),
    .w_mdata(w_mdata), .w_rd(w_rd), .w_res(mem_wb_1_w_res));
  Multiplexer #(.width(32), .select(1)) multiplexer_14 (
    .in0(mem_wb_1_w_res), .in1(w_mdata), .out(w_data), .sel(w_MemRead));

  // Other names for the same wires on the sheet: m_res[1:0] = m_boff; pc[31:0] = PC_out; redir = FLUSH; w_Halt = halt

  // Notes on the sheet:
  //   PC next / Counters
  //   IF + BTB
  //   contents of IMEM (hex, n*v repeats v):
  //   93 100113 193 c00213 11a023 2082b3 10093 28113 418193 fff20213 fe0214e3 313 193 c00213 1a383 730333
  //   418193 fff20213 fe0218e3 73
  //   IMEM
  //   IF/ID
  //   ID
  //   ID/EX
  //   EX
  //   ALU/M/F/CSR
  //   EX/MEM
  //   MEM: DMEM/D-cache/MMIO
  //   MEM/WB
  //   WB / outputs
endmodule

module ALU (
  input  [31:0] a,
  input  [31:0] b,
  input  [3:0] op,
  output [31:0] y
);

  wire comparator_1_lt, comparator_2_lt;
  wire [31:0] add, \and , bit_extender_1_out, bit_extender_2_out, \or , shifter_1_out, shifter_2_out,
       shifter_3_out, sub, \xor ;

  Adder #(.width(32)) adder_1 (.a(a), .b(b), .out(add));  // open: cin, cout
  Subtractor #(.width(32)) subtractor_1 (.a(a), .b(b), .out(sub));  // open: bin, bout
  Comparator #(.width(32), .mode("twosComplement")) comparator_1 (.a(a), .b(b), .lt(comparator_1_lt));  // open: gt, eq
  Comparator #(.width(32), .mode("unsigned")) comparator_2 (.a(a), .b(b), .lt(comparator_2_lt));  // open: gt, eq
  assign \xor  = a ^ b;  // XOR_Gate xor_1, 32 bits wide
  assign \or  = a | b;  // OR_Gate or_1, 32 bits wide
  assign \and  = a & b;  // AND_Gate and_1, 32 bits wide
  Shifter #(.width(32), .shift("ll")) shifter_1 (.in(a), .\dist (b[4:0]), .out(shifter_1_out));
  Shifter #(.width(32), .shift("lr")) shifter_2 (.in(a), .\dist (b[4:0]), .out(shifter_2_out));
  Shifter #(.width(32), .shift("ar")) shifter_3 (.in(a), .\dist (b[4:0]), .out(shifter_3_out));
  assign bit_extender_1_out = {{31{1'b0}}, comparator_1_lt};  // Bit_Extender bit_extender_1
  assign bit_extender_2_out = {{31{1'b0}}, comparator_2_lt};  // Bit_Extender bit_extender_2
  Multiplexer #(.width(32), .select(4)) multiplexer_1 (
    .in0(add), .in1(sub), .in2(shifter_1_out), .in3(bit_extender_1_out), .in4(bit_extender_2_out),
    .in5(\xor ), .in6(shifter_2_out), .in7(shifter_3_out), .in8(\or ), .in9(\and ), .in10({32{1'b0}}),
    .in11({32{1'b0}}), .in12({32{1'b0}}), .in13({32{1'b0}}), .in14({32{1'b0}}), .in15({32{1'b0}}), .out(y),
    .sel(op));
endmodule

module RegFile64 (
  input  clk,
  input  we,
  input  [5:0] rs1,
  input  [5:0] rs2,
  input  [5:0] rd,
  input  [31:0] wd,
  output [31:0] r1,
  output [31:0] r2
);

  wire and_2_out, and_3_out, and_4_out, and_5_out, and_6_out, and_7_out, and_8_out, and_9_out, and_10_out,
       and_11_out, and_12_out, and_13_out, and_14_out, and_15_out, and_16_out, and_17_out, and_18_out,
       and_19_out, and_20_out, and_21_out, and_22_out, and_23_out, and_24_out, and_25_out, and_26_out,
       and_27_out, and_28_out, and_29_out, and_30_out, and_31_out, and_32_out, and_33_out, and_34_out,
       and_35_out, and_36_out, and_37_out, and_38_out, and_39_out, and_40_out, and_41_out, and_42_out,
       and_43_out, and_44_out, and_45_out, and_46_out, and_47_out, and_48_out, and_49_out, and_50_out,
       and_51_out, and_52_out, and_53_out, and_54_out, and_55_out, and_56_out, and_57_out, and_58_out,
       and_59_out, and_60_out, and_61_out, and_62_out, and_63_out, and_64_out, and_65_out, and_66_out,
       and_67_out, and_68_out, and_69_out, and_70_out, and_71_out, and_72_out, and_73_out, and_74_out,
       and_75_out, and_76_out, and_77_out, and_78_out, and_79_out, and_80_out, and_81_out, and_82_out,
       and_83_out, and_84_out, and_85_out, and_86_out, and_87_out, and_88_out, and_89_out, and_90_out,
       and_91_out, and_92_out, and_93_out, and_94_out, and_95_out, and_96_out, and_97_out, and_98_out,
       and_99_out, and_100_out, and_101_out, and_102_out, and_103_out, and_104_out, and_105_out, and_106_out,
       and_107_out, and_108_out, and_109_out, and_110_out, and_111_out, and_112_out, and_113_out,
       and_114_out, and_115_out, and_116_out, and_117_out, and_118_out, and_119_out, and_120_out,
       and_121_out, and_122_out, and_123_out, and_124_out, and_125_out, and_126_out, and_127_out,
       decoder_1_out4, decoder_1_out5, decoder_1_out6, decoder_1_out7, decoder_1_out8, decoder_1_out9,
       decoder_1_out10, decoder_1_out12, decoder_1_out13, decoder_1_out14, decoder_1_out15, decoder_1_out16,
       decoder_1_out17, decoder_1_out18, decoder_1_out20, decoder_1_out21, decoder_1_out22, decoder_1_out23,
       decoder_1_out24, decoder_1_out25, decoder_1_out26, decoder_1_out28, decoder_1_out29, decoder_1_out30,
       decoder_1_out31, dl0, dl1, dl2, dl3, dl11, dl19, dl27, nrdh;
  wire [31:0] multiplexer_1_out, multiplexer_2_out, multiplexer_3_out, multiplexer_4_out, register_4_q,
       register_7_q, register_8_q, register_15_q, register_16_q, register_17_q, register_19_q, register_20_q,
       register_21_q, register_22_q, register_23_q, register_24_q, register_25_q, register_27_q,
       register_28_q, register_29_q, register_31_q, register_32_q, register_33_q, register_35_q,
       register_36_q, register_37_q, register_38_q, register_39_q, register_40_q, register_41_q,
       register_43_q, register_44_q, register_45_q, register_47_q, register_48_q, register_49_q,
       register_50_q, register_51_q, register_52_q, register_53_q, register_55_q, register_56_q,
       register_57_q, register_59_q, register_60_q, register_61_q, register_62_q, register_63_q, x1, x2, x3,
       x5, x6, x9, x10, x11, x12, x13, x14, x18, x26, x30, x34, x42, x46, x54, x58;

  not not_1 (nrdh, rd[5]);
  Decoder #(.select(5), .enable("false")) decoder_1 (
    .out0(dl0), .out1(dl1), .out2(dl2), .out3(dl3), .out4(decoder_1_out4), .out5(decoder_1_out5),
    .out6(decoder_1_out6), .out7(decoder_1_out7), .out8(decoder_1_out8), .out9(decoder_1_out9),
    .out10(decoder_1_out10), .out11(dl11), .out12(decoder_1_out12), .out13(decoder_1_out13),
    .out14(decoder_1_out14), .out15(decoder_1_out15), .out16(decoder_1_out16), .out17(decoder_1_out17),
    .out18(decoder_1_out18), .out19(dl19), .out20(decoder_1_out20), .out21(decoder_1_out21),
    .out22(decoder_1_out22), .out23(decoder_1_out23), .out24(decoder_1_out24), .out25(decoder_1_out25),
    .out26(decoder_1_out26), .out27(dl27), .out28(decoder_1_out28), .out29(decoder_1_out29),
    .out30(decoder_1_out30), .out31(decoder_1_out31), .sel(rd[4:0]));
  // AND_Gate and_1 has open pins: in0=dl0, in1=nrdh, out=open
  and and_2 (and_2_out, dl0, rd[5]);
  and and_3 (and_3_out, dl1, nrdh);
  and and_4 (and_4_out, dl1, rd[5]);
  and and_5 (and_5_out, dl2, nrdh);
  and and_6 (and_6_out, dl2, rd[5]);
  and and_7 (and_7_out, dl3, nrdh);
  and and_8 (and_8_out, dl3, rd[5]);
  and and_9 (and_9_out, decoder_1_out4, nrdh);
  and and_10 (and_10_out, decoder_1_out4, rd[5]);
  and and_11 (and_11_out, decoder_1_out5, nrdh);
  and and_12 (and_12_out, decoder_1_out5, rd[5]);
  and and_13 (and_13_out, decoder_1_out6, nrdh);
  and and_14 (and_14_out, decoder_1_out6, rd[5]);
  and and_15 (and_15_out, decoder_1_out7, nrdh);
  and and_16 (and_16_out, decoder_1_out7, rd[5]);
  and and_17 (and_17_out, decoder_1_out8, nrdh);
  and and_18 (and_18_out, decoder_1_out8, rd[5]);
  and and_19 (and_19_out, decoder_1_out9, nrdh);
  and and_20 (and_20_out, decoder_1_out9, rd[5]);
  and and_21 (and_21_out, decoder_1_out10, nrdh);
  and and_22 (and_22_out, decoder_1_out10, rd[5]);
  and and_23 (and_23_out, dl11, nrdh);
  and and_24 (and_24_out, dl11, rd[5]);
  and and_25 (and_25_out, decoder_1_out12, nrdh);
  and and_26 (and_26_out, decoder_1_out12, rd[5]);
  and and_27 (and_27_out, decoder_1_out13, nrdh);
  and and_28 (and_28_out, decoder_1_out13, rd[5]);
  and and_29 (and_29_out, decoder_1_out14, nrdh);
  and and_30 (and_30_out, decoder_1_out14, rd[5]);
  and and_31 (and_31_out, decoder_1_out15, nrdh);
  and and_32 (and_32_out, decoder_1_out15, rd[5]);
  and and_33 (and_33_out, decoder_1_out16, nrdh);
  and and_34 (and_34_out, decoder_1_out16, rd[5]);
  and and_35 (and_35_out, decoder_1_out17, nrdh);
  and and_36 (and_36_out, decoder_1_out17, rd[5]);
  and and_37 (and_37_out, decoder_1_out18, nrdh);
  and and_38 (and_38_out, decoder_1_out18, rd[5]);
  and and_39 (and_39_out, dl19, nrdh);
  and and_40 (and_40_out, dl19, rd[5]);
  and and_41 (and_41_out, decoder_1_out20, nrdh);
  and and_42 (and_42_out, decoder_1_out20, rd[5]);
  and and_43 (and_43_out, decoder_1_out21, nrdh);
  and and_44 (and_44_out, decoder_1_out21, rd[5]);
  and and_45 (and_45_out, decoder_1_out22, nrdh);
  and and_46 (and_46_out, decoder_1_out22, rd[5]);
  and and_47 (and_47_out, decoder_1_out23, nrdh);
  and and_48 (and_48_out, decoder_1_out23, rd[5]);
  and and_49 (and_49_out, decoder_1_out24, nrdh);
  and and_50 (and_50_out, decoder_1_out24, rd[5]);
  and and_51 (and_51_out, decoder_1_out25, nrdh);
  and and_52 (and_52_out, decoder_1_out25, rd[5]);
  and and_53 (and_53_out, decoder_1_out26, nrdh);
  and and_54 (and_54_out, decoder_1_out26, rd[5]);
  and and_55 (and_55_out, dl27, nrdh);
  and and_56 (and_56_out, dl27, rd[5]);
  and and_57 (and_57_out, decoder_1_out28, nrdh);
  and and_58 (and_58_out, decoder_1_out28, rd[5]);
  and and_59 (and_59_out, decoder_1_out29, nrdh);
  and and_60 (and_60_out, decoder_1_out29, rd[5]);
  and and_61 (and_61_out, decoder_1_out30, nrdh);
  and and_62 (and_62_out, decoder_1_out30, rd[5]);
  and and_63 (and_63_out, decoder_1_out31, nrdh);
  and and_64 (and_64_out, decoder_1_out31, rd[5]);
  and and_65 (and_65_out, we, and_3_out);
  and and_66 (and_66_out, we, and_5_out);
  and and_67 (and_67_out, we, and_7_out);
  and and_68 (and_68_out, we, and_9_out);
  and and_69 (and_69_out, we, and_11_out);
  and and_70 (and_70_out, we, and_13_out);
  and and_71 (and_71_out, we, and_15_out);
  and and_72 (and_72_out, we, and_17_out);
  and and_73 (and_73_out, we, and_19_out);
  and and_74 (and_74_out, we, and_21_out);
  and and_75 (and_75_out, we, and_23_out);
  and and_76 (and_76_out, we, and_25_out);
  and and_77 (and_77_out, we, and_27_out);
  and and_78 (and_78_out, we, and_29_out);
  and and_79 (and_79_out, we, and_31_out);
  and and_80 (and_80_out, we, and_33_out);
  and and_81 (and_81_out, we, and_35_out);
  and and_82 (and_82_out, we, and_37_out);
  and and_83 (and_83_out, we, and_39_out);
  and and_84 (and_84_out, we, and_41_out);
  and and_85 (and_85_out, we, and_43_out);
  and and_86 (and_86_out, we, and_45_out);
  and and_87 (and_87_out, we, and_47_out);
  and and_88 (and_88_out, we, and_49_out);
  and and_89 (and_89_out, we, and_51_out);
  and and_90 (and_90_out, we, and_53_out);
  and and_91 (and_91_out, we, and_55_out);
  and and_92 (and_92_out, we, and_57_out);
  and and_93 (and_93_out, we, and_59_out);
  and and_94 (and_94_out, we, and_61_out);
  and and_95 (and_95_out, we, and_63_out);
  and and_96 (and_96_out, we, and_2_out);
  and and_97 (and_97_out, we, and_4_out);
  and and_98 (and_98_out, we, and_6_out);
  and and_99 (and_99_out, we, and_8_out);
  and and_100 (and_100_out, we, and_10_out);
  and and_101 (and_101_out, we, and_12_out);
  and and_102 (and_102_out, we, and_14_out);
  and and_103 (and_103_out, we, and_16_out);
  and and_104 (and_104_out, we, and_18_out);
  and and_105 (and_105_out, we, and_20_out);
  and and_106 (and_106_out, we, and_22_out);
  and and_107 (and_107_out, we, and_24_out);
  and and_108 (and_108_out, we, and_26_out);
  and and_109 (and_109_out, we, and_28_out);
  and and_110 (and_110_out, we, and_30_out);
  and and_111 (and_111_out, we, and_32_out);
  and and_112 (and_112_out, we, and_34_out);
  and and_113 (and_113_out, we, and_36_out);
  and and_114 (and_114_out, we, and_38_out);
  and and_115 (and_115_out, we, and_40_out);
  and and_116 (and_116_out, we, and_42_out);
  and and_117 (and_117_out, we, and_44_out);
  and and_118 (and_118_out, we, and_46_out);
  and and_119 (and_119_out, we, and_48_out);
  and and_120 (and_120_out, we, and_50_out);
  and and_121 (and_121_out, we, and_52_out);
  and and_122 (and_122_out, we, and_54_out);
  and and_123 (and_123_out, we, and_56_out);
  and and_124 (and_124_out, we, and_58_out);
  and and_125 (and_125_out, we, and_60_out);
  and and_126 (and_126_out, we, and_62_out);
  and and_127 (and_127_out, we, and_64_out);
  Register #(.width(32)) register_1 (.D(wd), .en(and_65_out), .clk(clk), .Q(x1));  // open: clr
  Register #(.width(32)) register_2 (.D(wd), .en(and_66_out), .clk(clk), .Q(x2));  // open: clr
  Register #(.width(32)) register_3 (.D(wd), .en(and_67_out), .clk(clk), .Q(x3));  // open: clr
  Register #(.width(32)) register_4 (.D(wd), .en(and_68_out), .clk(clk), .Q(register_4_q));  // open: clr
  Register #(.width(32)) register_5 (.D(wd), .en(and_69_out), .clk(clk), .Q(x5));  // open: clr
  Register #(.width(32)) register_6 (.D(wd), .en(and_70_out), .clk(clk), .Q(x6));  // open: clr
  Register #(.width(32)) register_7 (.D(wd), .en(and_71_out), .clk(clk), .Q(register_7_q));  // open: clr
  Register #(.width(32)) register_8 (.D(wd), .en(and_72_out), .clk(clk), .Q(register_8_q));  // open: clr
  Register #(.width(32)) register_9 (.D(wd), .en(and_73_out), .clk(clk), .Q(x9));  // open: clr
  Register #(.width(32)) register_10 (.D(wd), .en(and_74_out), .clk(clk), .Q(x10));  // open: clr
  Register #(.width(32)) register_11 (.D(wd), .en(and_75_out), .clk(clk), .Q(x11));  // open: clr
  Register #(.width(32)) register_12 (.D(wd), .en(and_76_out), .clk(clk), .Q(x12));  // open: clr
  Register #(.width(32)) register_13 (.D(wd), .en(and_77_out), .clk(clk), .Q(x13));  // open: clr
  Register #(.width(32)) register_14 (.D(wd), .en(and_78_out), .clk(clk), .Q(x14));  // open: clr
  Register #(.width(32)) register_15 (.D(wd), .en(and_79_out), .clk(clk), .Q(register_15_q));  // open: clr
  Register #(.width(32)) register_16 (.D(wd), .en(and_80_out), .clk(clk), .Q(register_16_q));  // open: clr
  Register #(.width(32)) register_17 (.D(wd), .en(and_81_out), .clk(clk), .Q(register_17_q));  // open: clr
  Register #(.width(32)) register_18 (.D(wd), .en(and_82_out), .clk(clk), .Q(x18));  // open: clr
  Register #(.width(32)) register_19 (.D(wd), .en(and_83_out), .clk(clk), .Q(register_19_q));  // open: clr
  Register #(.width(32)) register_20 (.D(wd), .en(and_84_out), .clk(clk), .Q(register_20_q));  // open: clr
  Register #(.width(32)) register_21 (.D(wd), .en(and_85_out), .clk(clk), .Q(register_21_q));  // open: clr
  Register #(.width(32)) register_22 (.D(wd), .en(and_86_out), .clk(clk), .Q(register_22_q));  // open: clr
  Register #(.width(32)) register_23 (.D(wd), .en(and_87_out), .clk(clk), .Q(register_23_q));  // open: clr
  Register #(.width(32)) register_24 (.D(wd), .en(and_88_out), .clk(clk), .Q(register_24_q));  // open: clr
  Register #(.width(32)) register_25 (.D(wd), .en(and_89_out), .clk(clk), .Q(register_25_q));  // open: clr
  Register #(.width(32)) register_26 (.D(wd), .en(and_90_out), .clk(clk), .Q(x26));  // open: clr
  Register #(.width(32)) register_27 (.D(wd), .en(and_91_out), .clk(clk), .Q(register_27_q));  // open: clr
  Register #(.width(32)) register_28 (.D(wd), .en(and_92_out), .clk(clk), .Q(register_28_q));  // open: clr
  Register #(.width(32)) register_29 (.D(wd), .en(and_93_out), .clk(clk), .Q(register_29_q));  // open: clr
  Register #(.width(32)) register_30 (.D(wd), .en(and_94_out), .clk(clk), .Q(x30));  // open: clr
  Register #(.width(32)) register_31 (.D(wd), .en(and_95_out), .clk(clk), .Q(register_31_q));  // open: clr
  Register #(.width(32)) register_32 (.D(wd), .en(and_96_out), .clk(clk), .Q(register_32_q));  // open: clr
  Register #(.width(32)) register_33 (.D(wd), .en(and_97_out), .clk(clk), .Q(register_33_q));  // open: clr
  Register #(.width(32)) register_34 (.D(wd), .en(and_98_out), .clk(clk), .Q(x34));  // open: clr
  Register #(.width(32)) register_35 (.D(wd), .en(and_99_out), .clk(clk), .Q(register_35_q));  // open: clr
  Register #(.width(32)) register_36 (.D(wd), .en(and_100_out), .clk(clk), .Q(register_36_q));  // open: clr
  Register #(.width(32)) register_37 (.D(wd), .en(and_101_out), .clk(clk), .Q(register_37_q));  // open: clr
  Register #(.width(32)) register_38 (.D(wd), .en(and_102_out), .clk(clk), .Q(register_38_q));  // open: clr
  Register #(.width(32)) register_39 (.D(wd), .en(and_103_out), .clk(clk), .Q(register_39_q));  // open: clr
  Register #(.width(32)) register_40 (.D(wd), .en(and_104_out), .clk(clk), .Q(register_40_q));  // open: clr
  Register #(.width(32)) register_41 (.D(wd), .en(and_105_out), .clk(clk), .Q(register_41_q));  // open: clr
  Register #(.width(32)) register_42 (.D(wd), .en(and_106_out), .clk(clk), .Q(x42));  // open: clr
  Register #(.width(32)) register_43 (.D(wd), .en(and_107_out), .clk(clk), .Q(register_43_q));  // open: clr
  Register #(.width(32)) register_44 (.D(wd), .en(and_108_out), .clk(clk), .Q(register_44_q));  // open: clr
  Register #(.width(32)) register_45 (.D(wd), .en(and_109_out), .clk(clk), .Q(register_45_q));  // open: clr
  Register #(.width(32)) register_46 (.D(wd), .en(and_110_out), .clk(clk), .Q(x46));  // open: clr
  Register #(.width(32)) register_47 (.D(wd), .en(and_111_out), .clk(clk), .Q(register_47_q));  // open: clr
  Register #(.width(32)) register_48 (.D(wd), .en(and_112_out), .clk(clk), .Q(register_48_q));  // open: clr
  Register #(.width(32)) register_49 (.D(wd), .en(and_113_out), .clk(clk), .Q(register_49_q));  // open: clr
  Register #(.width(32)) register_50 (.D(wd), .en(and_114_out), .clk(clk), .Q(register_50_q));  // open: clr
  Register #(.width(32)) register_51 (.D(wd), .en(and_115_out), .clk(clk), .Q(register_51_q));  // open: clr
  Register #(.width(32)) register_52 (.D(wd), .en(and_116_out), .clk(clk), .Q(register_52_q));  // open: clr
  Register #(.width(32)) register_53 (.D(wd), .en(and_117_out), .clk(clk), .Q(register_53_q));  // open: clr
  Register #(.width(32)) register_54 (.D(wd), .en(and_118_out), .clk(clk), .Q(x54));  // open: clr
  Register #(.width(32)) register_55 (.D(wd), .en(and_119_out), .clk(clk), .Q(register_55_q));  // open: clr
  Register #(.width(32)) register_56 (.D(wd), .en(and_120_out), .clk(clk), .Q(register_56_q));  // open: clr
  Register #(.width(32)) register_57 (.D(wd), .en(and_121_out), .clk(clk), .Q(register_57_q));  // open: clr
  Register #(.width(32)) register_58 (.D(wd), .en(and_122_out), .clk(clk), .Q(x58));  // open: clr
  Register #(.width(32)) register_59 (.D(wd), .en(and_123_out), .clk(clk), .Q(register_59_q));  // open: clr
  Register #(.width(32)) register_60 (.D(wd), .en(and_124_out), .clk(clk), .Q(register_60_q));  // open: clr
  Register #(.width(32)) register_61 (.D(wd), .en(and_125_out), .clk(clk), .Q(register_61_q));  // open: clr
  Register #(.width(32)) register_62 (.D(wd), .en(and_126_out), .clk(clk), .Q(register_62_q));  // open: clr
  Register #(.width(32)) register_63 (.D(wd), .en(and_127_out), .clk(clk), .Q(register_63_q));  // open: clr
  Multiplexer #(.width(32), .select(5)) multiplexer_1 (
    .in0({32{1'b0}}), .in1(x1), .in2(x2), .in3(x3), .in4(register_4_q), .in5(x5), .in6(x6),
    .in7(register_7_q), .in8(register_8_q), .in9(x9), .in10(x10), .in11(x11), .in12(x12), .in13(x13),
    .in14(x14), .in15(register_15_q), .in16(register_16_q), .in17(register_17_q), .in18(x18),
    .in19(register_19_q), .in20(register_20_q), .in21(register_21_q), .in22(register_22_q),
    .in23(register_23_q), .in24(register_24_q), .in25(register_25_q), .in26(x26), .in27(register_27_q),
    .in28(register_28_q), .in29(register_29_q), .in30(x30), .in31(register_31_q), .out(multiplexer_1_out),
    .sel(rs1[4:0]));
  Multiplexer #(.width(32), .select(5)) multiplexer_2 (
    .in0(register_32_q), .in1(register_33_q), .in2(x34), .in3(register_35_q), .in4(register_36_q),
    .in5(register_37_q), .in6(register_38_q), .in7(register_39_q), .in8(register_40_q), .in9(register_41_q),
    .in10(x42), .in11(register_43_q), .in12(register_44_q), .in13(register_45_q), .in14(x46),
    .in15(register_47_q), .in16(register_48_q), .in17(register_49_q), .in18(register_50_q),
    .in19(register_51_q), .in20(register_52_q), .in21(register_53_q), .in22(x54), .in23(register_55_q),
    .in24(register_56_q), .in25(register_57_q), .in26(x58), .in27(register_59_q), .in28(register_60_q),
    .in29(register_61_q), .in30(register_62_q), .in31(register_63_q), .out(multiplexer_2_out), .sel(rs1[4:0]));
  Multiplexer #(.width(32), .select(5)) multiplexer_3 (
    .in0({32{1'b0}}), .in1(x1), .in2(x2), .in3(x3), .in4(register_4_q), .in5(x5), .in6(x6),
    .in7(register_7_q), .in8(register_8_q), .in9(x9), .in10(x10), .in11(x11), .in12(x12), .in13(x13),
    .in14(x14), .in15(register_15_q), .in16(register_16_q), .in17(register_17_q), .in18(x18),
    .in19(register_19_q), .in20(register_20_q), .in21(register_21_q), .in22(register_22_q),
    .in23(register_23_q), .in24(register_24_q), .in25(register_25_q), .in26(x26), .in27(register_27_q),
    .in28(register_28_q), .in29(register_29_q), .in30(x30), .in31(register_31_q), .out(multiplexer_3_out),
    .sel(rs2[4:0]));
  Multiplexer #(.width(32), .select(5)) multiplexer_4 (
    .in0(register_32_q), .in1(register_33_q), .in2(x34), .in3(register_35_q), .in4(register_36_q),
    .in5(register_37_q), .in6(register_38_q), .in7(register_39_q), .in8(register_40_q), .in9(register_41_q),
    .in10(x42), .in11(register_43_q), .in12(register_44_q), .in13(register_45_q), .in14(x46),
    .in15(register_47_q), .in16(register_48_q), .in17(register_49_q), .in18(register_50_q),
    .in19(register_51_q), .in20(register_52_q), .in21(register_53_q), .in22(x54), .in23(register_55_q),
    .in24(register_56_q), .in25(register_57_q), .in26(x58), .in27(register_59_q), .in28(register_60_q),
    .in29(register_61_q), .in30(register_62_q), .in31(register_63_q), .out(multiplexer_4_out), .sel(rs2[4:0]));
  Multiplexer #(.width(32), .select(1)) multiplexer_5 (
    .in0(multiplexer_1_out), .in1(multiplexer_2_out), .out(r1), .sel(rs1[5]));
  Multiplexer #(.width(32), .select(1)) multiplexer_6 (
    .in0(multiplexer_3_out), .in1(multiplexer_4_out), .out(r2), .sel(rs2[5]));

  // Other names for the same wires on the sheet: rdl[4:0] = rd[4:0]; rdh = rd[5]; s1l[4:0] = rs1[4:0]; s1h = rs1[5];
  //   s2l[4:0] = rs2[4:0]; s2h = rs2[5]
endmodule

module ImmGen (
  input  [31:0] instr,
  input  [2:0] sel,
  output [31:0] imm
);

  wire [31:0] bit_extender_2_out, bit_extender_3_out, bit_extender_4_out, immI;

  assign immI = {{20{instr[31]}}, instr[31:20]};  // Bit_Extender bit_extender_1
  assign bit_extender_2_out = {{20{instr[31]}}, {instr[31:25], instr[11:7]}};  // Bit_Extender bit_extender_2
  assign bit_extender_3_out = {{19{instr[31]}}, {instr[31], instr[7], instr[30:25], instr[11:8], 1'b0}};  // Bit_Extender bit_extender_3
  assign bit_extender_4_out = {{11{instr[31]}}, {instr[31], instr[19:12], instr[20], instr[30:21], 1'b0}};  // Bit_Extender bit_extender_4
  Multiplexer #(.width(32), .select(3)) multiplexer_1 (
    .in0(immI), .in1(bit_extender_2_out), .in2(bit_extender_3_out), .in3({instr[31:12], {12{1'b0}}}),
    .in4(bit_extender_4_out), .in5({32{1'b0}}), .in6({32{1'b0}}), .in7({32{1'b0}}), .out(imm), .sel(sel));

  // Other names for the same wires on the sheet: b4_1[3:0] = instr[11:8];
  //   b13[12:1] = {instr[31], instr[7], instr[30:25], instr[11:8]}; s12[11:0] = {instr[31:25], instr[11:7]};
  //   s_lo[4:0] = instr[11:7]; b11 = instr[7]; immU[31:12] = instr[31:12]; j10_1[9:0] = instr[30:21];
  //   j21[20:1] = {instr[31], instr[19:12], instr[20], instr[30:21]}; u20[19:0] = instr[31:12];
  //   b10_5[5:0] = instr[30:25]; s_hi[6:0] = instr[31:25]; j11 = instr[20]; j19_12[7:0] = instr[19:12];
  //   b12 = instr[31]
endmodule

module BranchUnit (
  input  [31:0] a,
  input  [31:0] b,
  input  [2:0] f3,
  output cond
);

  wire eq, lts, ltu, not_1_out, not_2_out, not_3_out;

  Comparator #(.width(32), .mode("twosComplement")) comparator_1 (.a(a), .b(b), .eq(eq), .lt(lts));  // open: gt
  Comparator #(.width(32), .mode("unsigned")) comparator_2 (.a(a), .b(b), .lt(ltu));  // open: gt, eq
  not not_1 (not_1_out, eq);
  not not_2 (not_2_out, lts);
  not not_3 (not_3_out, ltu);
  Multiplexer #(.width(1), .select(3)) multiplexer_1 (
    .in0(eq), .in1(not_1_out), .in2(1'b0), .in3(1'b0), .in4(lts), .in5(not_2_out), .in6(ltu),
    .in7(not_3_out), .out(cond), .sel(f3));
endmodule

module Control (
  input  [31:0] instr,
  output [31:0] ctrl
);

  wire qok;
  wire [31:0] CTRL_data;

  and and_1 (qok, instr[0], instr[1]);
  ROM #(.addrWidth(16), .dataWidth(32)) u_CTRL (
    .addr({instr[20], instr[31:25], instr[14:12], instr[6:2]}), .data(CTRL_data));
  Multiplexer #(.width(32), .select(1)) multiplexer_1 (.in0({32{1'b0}}), .in1(CTRL_data), .out(ctrl), .sel(qok));

  // Other names for the same wires on the sheet: caddr[15:0] = {instr[20], instr[31:25], instr[14:12], instr[6:2]};
  //   op5[4:0] = instr[6:2]; f3[2:0] = instr[14:12]; f7[6:0] = instr[31:25]; b20 = instr[20]

  // Notes on the sheet:
  //   contents of CTRL (hex, n*v repeats v):
  //   500109 3*0 500009 40600b 2*0 702208 3*0 700001 40600d 6*0 e0701001 3*0 714000 540409 0 428401 480000
  //   3*0 500109 3*0 500029 40600b 2*0 702208 3*0 700021 40600d 6*0 e0701001 3*0 714000 2*0 428401 d00c01
  //   3*0 500109 20500109 2*0 500039 40600b 2*0 702208 80702208 2*0 700031 40600d 6*0 e0701001 6*0 428401
  //   d00c01 7*0 500049 40600b 6*0 700041 40600d 6*0 e0701001 6*0 428401 d00c01 3*0 500109 3*0 500059
  //   40600b 6*0 700051 40600d 6*0 e0701001 3*0 714000 2*0 428401 4*0 500109 3*0 500069 40600b 6*0 700061
  //   40600d 6*0 e0701001 3*0 714000 2*0 428401 c00c01 7*0 500089 40600b 6*0 700081 40600d 6*0 e0701001
  //   3*0 714000 2*0 428401 c00c01 7*0 500099 40600b 6*0 700091 40600d 6*0 e0701001 3*0 714000 2*0 428401
  //   c00c01 3*0 500109 3*0 500009 40600b 2*0 702208 3*0 700801 40600d 10*0 714000 540409 0 428401 480000
  //   3*0 500109 4*0 40600b 2*0 702208 3*0 700801 40600d 10*0 714000 2*0 428401 d00c01 3*0 500109 20500109
  //   2*0 500039 40600b 2*0 702208 80702208 2*0 700801 40600d 13*0 428401 d00c01 7*0 500049 40600b 6*0
  //   700801 40600d 13*0 428401 d00c01 3*0 500109 3*0 500059 40600b 6*0 700801 40600d 10*0 714000 2*0
  //   428401 4*0 500109 4*0 40600b 6*0 700801 40600d 10*0 714000 2*0 428401 c00c01 7*0 500089 40600b 6*0
  //   700801 40600d 10*0 714000 2*0 428401 c00c01 7*0 500099 40600b 6*0 700801 40600d 10*0 714000 2*0
  //   428401 c00c01 3*0 500109 3*0 500009 40600b 2*0 702208 4*0 40600d 10*0 714000 540409 0 428401 480000
  //   3*0 500109 4*0 40600b 2*0 702208 4*0 40600d 10*0 714000 2*0 428401 d00c01 3*0 500109 20500109 2*0
  //   500039 40600b 2*0 702208 80702208 3*0 40600d 13*0 428401 d00c01 7*0 500049 40600b 7*0 40600d 13*0
  //   428401 d00c01 3*0 500109 3*0 500059 40600b 7*0 40600d 10*0 714000 2*0 428401 4*0 500109 4*0 40600b
  //   7*0 40600d 10*0 714000 2*0 428401 c00c01 7*0 500089 40600b 7*0 40600d 10*0 714000 2*0 428401 c00c01
  //   7*0 500099 40600b 7*0 40600d 10*0 714000 2*0 428401 c00c01 3*0 500109 3*0 500009 40600b 2*0 702208
  //   4*0 40600d 10*0 714000 540409 0 428401 480000 3*0 500109 4*0 40600b 2*0 702208 4*0 40600d 10*0
  //   714000 2*0 428401 d00c01 3*0 500109 20500109 2*0 500039 40600b 2*0 702208 80702208 3*0 40600d 13*0
  //   428401 d00c01 7*0 500049 40600b 7*0 40600d 13*0 428401 d00c01 3*0 500109 3*0 500059 40600b 7*0
  //   40600d 10*0 714000 2*0 428401 4*0 500109 4*0 40600b 7*0 40600d 10*0 714000 2*0 428401 c00c01 7*0
  //   500089 40600b 7*0 40600d 10*0 714000 2*0 428401 c00c01 7*0 500099 40600b 7*0 40600d 10*0 714000 2*0
  //   428401 c00c01 3*0 500109 3*0 500009 40600b 2*0 702208 4*0 40600d 6*0 e2701001 3*0 714000 540409 0
  //   428401 480000 3*0 500109 4*0 40600b 2*0 702208 4*0 40600d 6*0 e2701001 3*0 714000 2*0 428401 d00c01
  //   3*0 500109 20500109 2*0 500039 40600b 2*0 702208 80702208 3*0 40600d 6*0 e2701001 6*0 428401 d00c01
  //   7*0 500049 40600b 7*0 40600d 6*0 e2701001 6*0 428401 d00c01 3*0 500109 3*0 500059 40600b 7*0 40600d
  //   6*0 e2701001 3*0 714000 2*0 428401 4*0 500109 4*0 40600b 7*0 40600d 6*0 e2701001 3*0 714000 2*0
  //   428401 c00c01 7*0 500089 40600b 7*0 40600d 6*0 e2701001 3*0 714000 2*0 428401 c00c01 7*0 500099
  //   40600b 7*0 40600d 6*0 e2701001 3*0 714000 2*0 428401 c00c01 3*0 500109 3*0 500009 40600b 2*0 702208
  //   4*0 40600d 10*0 714000 540409 0 428401 480000 3*0 500109 4*0 40600b 2*0 702208 4*0 40600d 10*0
  //   714000 2*0 428401 d00c01 3*0 500109 20500109 2*0 500039 40600b 2*0 702208 80702208 3*0 40600d 13*0
  //   428401 d00c01 7*0 500049 40600b 7*0 40600d 13*0 428401 d00c01 3*0 500109 3*0 500059 40600b 7*0
  //   40600d 10*0 714000 2*0 428401 4*0 500109 4*0 40600b 7*0 40600d 10*0 714000 2*0 428401 c00c01 7*0
  //   500089 40600b 7*0 40600d 10*0 714000 2*0 428401 c00c01 7*0 500099 40600b 7*0 40600d 10*0 714000 2*0
  //   428401 c00c01 3*0 500109 3*0 500009 40600b 2*0 702208 4*0 40600d 10*0 714000 540409 0 428401 480000
  //   3*0 500109 4*0 40600b 2*0 702208 4*0 40600d 10*0 714000 2*0 428401 d00c01 3*0 500109 20500109 2*0
  //   500039 40600b 2*0 702208 80702208 3*0 40600d 13*0 428401 d00c01 7*0 500049 40600b 7*0 40600d 13*0
  //   428401 d00c01 3*0 500109 3*0 500059 40600b 7*0 40600d 10*0 714000 2*0 428401 4*0 500109 4*0 40600b
  //   7*0 40600d 10*0 714000 2*0 428401 c00c01 7*0 500089 40600b 7*0 40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
endmodule

module LoadUnit (
  input  [31:0] din,
  input  [1:0] off,
  input  [2:0] f3,
  output [31:0] v
);

  wire [31:0] bit_extender_2_out, bit_extender_4_out, sb, sh16, x;

  Shifter #(.width(32), .shift("lr")) shifter_1 (.in(din), .\dist ({off, 3'b000}), .out(x));
  assign sb = {{24{x[7]}}, x[7:0]};  // Bit_Extender bit_extender_1
  assign bit_extender_2_out = {{24{1'b0}}, x[7:0]};  // Bit_Extender bit_extender_2
  assign sh16 = {{16{x[15]}}, x[15:0]};  // Bit_Extender bit_extender_3
  assign bit_extender_4_out = {{16{1'b0}}, x[15:0]};  // Bit_Extender bit_extender_4
  Multiplexer #(.width(32), .select(3)) multiplexer_1 (
    .in0(sb), .in1(sh16), .in2(x), .in3(x), .in4(bit_extender_2_out), .in5(bit_extender_4_out), .in6(x),
    .in7(x), .out(v), .sel(f3));

  // Other names for the same wires on the sheet: sh[4:3] = off
endmodule

module StoreUnit (
  input  [31:0] old,
  input  [31:0] wd,
  input  [1:0] off,
  input  [2:0] f3,
  output [31:0] \new 
);

  wire [31:0] and_2_out, ins, multiplexer_1_out, not_1_out, shifter_2_out, wds;

  Multiplexer #(.width(32), .select(2)) multiplexer_1 (
    .in0(32'hff), .in1(32'hffff), .in2({32{1'b1}}), .in3({32{1'b1}}), .out(multiplexer_1_out), .sel(f3[1:0]));
  Shifter #(.width(32), .shift("ll")) shifter_1 (.in(wd), .\dist ({off, 3'b000}), .out(wds));
  Shifter #(.width(32), .shift("ll")) shifter_2 (.in(multiplexer_1_out), .\dist ({off, 3'b000}), .out(shifter_2_out));
  assign not_1_out = ~shifter_2_out;  // NOT_Gate not_1, 32 bits wide
  assign ins = wds & shifter_2_out;  // AND_Gate and_1, 32 bits wide
  assign and_2_out = old & not_1_out;  // AND_Gate and_2, 32 bits wide
  assign \new  = and_2_out | ins;  // OR_Gate or_1, 32 bits wide

  // Other names for the same wires on the sheet: sz[1:0] = f3[1:0]; sh[4:3] = off
endmodule

module MulDiv (
  input  [31:0] a,
  input  [31:0] b,
  input  [2:0] f3,
  output [31:0] y
);

  wire bz;
  wire [31:0] asx, divider_1_out, divider_2_out, hiss, hisu, hiuu, lo, multiplexer_3_out, multiplexer_4_out,
       qu2, rs, ru, ru2;

  Multiplier #(.width(32), .mode("unsigned")) multiplier_1 (.a(a), .b(b), .out(lo), .cout(hiuu));  // open: cin
  Multiplier #(.width(32), .mode("twosComplement")) multiplier_2 (.a(a), .b(b), .cout(hiss));  // open: out, cin
  Multiplier #(.width(32), .mode("signedUnsigned")) multiplier_3 (.a(a), .b(b), .cout(hisu));  // open: out, cin
  Divider #(.width(32), .mode("unsigned")) divider_1 (.a(a), .b(b), .out(divider_1_out), .upper({32{1'b0}}), .rem(ru));
  Comparator #(.width(32), .mode("unsigned")) comparator_1 (.a(b), .b({32{1'b0}}), .eq(bz));  // open: gt, lt
  assign asx = {{31{a[31]}}, a[31]};  // Bit_Extender bit_extender_1
  Multiplexer #(.width(32), .select(1)) multiplexer_1 (.in0(divider_1_out), .in1({32{1'b1}}), .out(qu2), .sel(bz));
  Multiplexer #(.width(32), .select(1)) multiplexer_2 (.in0(ru), .in1(a), .out(ru2), .sel(bz));
  Divider #(.width(32), .mode("twosComplement")) divider_2 (.a(a), .b(b), .out(divider_2_out), .upper(asx), .rem(rs));
  Multiplexer #(.width(32), .select(1)) multiplexer_3 (
    .in0(divider_2_out), .in1({32{1'b1}}), .out(multiplexer_3_out), .sel(bz));
  Multiplexer #(.width(32), .select(1)) multiplexer_4 (.in0(rs), .in1(a), .out(multiplexer_4_out), .sel(bz));
  Multiplexer #(.width(32), .select(3)) multiplexer_5 (
    .in0(lo), .in1(hiss), .in2(hisu), .in3(hiuu), .in4(multiplexer_3_out), .in5(qu2),
    .in6(multiplexer_4_out), .in7(ru2), .out(y), .sel(f3));
endmodule

module FPU (
  input  [31:0] a,
  input  [31:0] b,
  input  [3:0] op,
  input  [2:0] rm,
  output [31:0] y
);

  wire feq, flt, multiplexer_4_out, not_1_out, or_1_out, xor_1_out;
  wire [31:0] bit_extender_1_out, fadd, fcvts, fcvtsu, fcvtw, fdiv, fminmax, fmul, fpminmax_1_p3,
       fpminmax_1_p4, fptoint_1_p2, fptoint_2_p2, fptoint_3_p2, fptoint_4_p2, fptoint_5_p2, fsqrt, fsub;
  wire [31:31] fsgnj;

  FPAdder #(.fpwidth(32)) fpadder_1 (.a(a), .b(b), .out(fadd));
  FPSubtractor #(.fpwidth(32)) fpsubtractor_1 (.a(a), .b(b), .out(fsub));
  FPMultiplier #(.fpwidth(32)) fpmultiplier_1 (.a(a), .b(b), .out(fmul));
  FPDivider #(.fpwidth(32)) fpdivider_1 (.a(a), .b(b), .out(fdiv));
  // FPSquareRoot #(.fpwidth(32)) fpsquareroot_1: pin names not known; wires that end beside it: a, fsqrt
  // FPMinMax #(.fpwidth(32)) fpminmax_1: pin names not known; wires that end beside it: a, b, fpminmax_1_p3, fpminmax_1_p4
  // FPComparator #(.fpwidth(32)) fpcomparator_1: pin names not known; wires that end beside it: a, b, feq, flt
  // FPToInt #(.width(32), .fpwidth(32), .mode("rint")) fptoint_1: pin names not known; wires that end beside it: a, fptoint_1_p2
  // FPToInt #(.width(32), .fpwidth(32), .mode("truncate")) fptoint_2: pin names not known; wires that end beside it: a, fptoint_2_p2
  // FPToInt #(.width(32), .fpwidth(32), .mode("floor")) fptoint_3: pin names not known; wires that end beside it: a, fptoint_3_p2
  // FPToInt #(.width(32), .fpwidth(32), .mode("ceil")) fptoint_4: pin names not known; wires that end beside it: a, fptoint_4_p2
  // FPToInt #(.width(32), .fpwidth(32), .mode("round")) fptoint_5: pin names not known; wires that end beside it: a, fptoint_5_p2
  // IntToFP #(.width(32), .fpwidth(32), .mode("twosComplement")) inttofp_1: pin names not known; wires that end beside it: a, fcvts
  // IntToFP #(.width(32), .fpwidth(32), .mode("unsigned")) inttofp_2: pin names not known; wires that end beside it: a, fcvtsu
  not not_1 (not_1_out, b[31]);
  xor xor_1 (xor_1_out, a[31], b[31]);
  Multiplexer #(.width(32), .select(1)) multiplexer_1 (
    .in0(fpminmax_1_p3), .in1(fpminmax_1_p4), .out(fminmax), .sel(rm[0]));
  or or_1 (or_1_out, flt, feq);
  Multiplexer #(.width(32), .select(3)) multiplexer_2 (
    .in0(fptoint_1_p2), .in1(fptoint_2_p2), .in2(fptoint_3_p2), .in3(fptoint_4_p2), .in4(fptoint_5_p2),
    .in5(fptoint_1_p2), .in6(fptoint_1_p2), .in7(fptoint_1_p2), .out(fcvtw), .sel(rm));
  Multiplexer #(.width(1), .select(2)) multiplexer_3 (
    .in0(b[31]), .in1(not_1_out), .in2(xor_1_out), .in3(b[31]), .out(fsgnj[31]), .sel(rm[1:0]));
  Multiplexer #(.width(1), .select(2)) multiplexer_4 (
    .in0(or_1_out), .in1(flt), .in2(feq), .in3(1'b0), .out(multiplexer_4_out), .sel(rm[1:0]));
  assign bit_extender_1_out = {{31{1'b0}}, multiplexer_4_out};  // Bit_Extender bit_extender_1
  Multiplexer #(.width(32), .select(4)) multiplexer_5 (
    .in0(fadd), .in1(fsub), .in2(fmul), .in3(fdiv), .in4(fsqrt), .in5({fsgnj[31], a[30:0]}), .in6(fminmax),
    .in7(bit_extender_1_out), .in8(fcvtw), .in9(fcvtw), .in10(fcvts), .in11(fcvtsu), .in12(a),
    .in13({32{1'b0}}), .in14({32{1'b0}}), .in15({32{1'b0}}), .out(y), .sel(op));

  // Other names for the same wires on the sheet: bs = b[31]; amag[30:0] = a[30:0]; fsgnj[30:0] = a[30:0];
  //   sj = fsgnj[31]; rm2[1:0] = rm[1:0]
endmodule

module BTB (
  input  clk,
  input  [31:0] rpc,
  input  we,
  input  [31:0] wpc,
  input  [31:0] wtgt,
  input  wtk,
  output ptk,
  output [31:0] ptgt
);

  wire and_1_out, and_2_out, and_3_out, and_4_out, and_5_out, and_6_out, and_7_out, and_8_out, and_9_out,
       and_10_out, and_11_out, and_12_out, and_13_out, and_14_out, and_15_out, comparator_1_eq,
       decoder_1_out3, decoder_1_out5, decoder_1_out6, decoder_1_out7, decoder_1_out8, decoder_1_out9,
       decoder_1_out10, decoder_1_out11, decoder_1_out13, decoder_1_out14, decoder_1_out15, e0, or_1_out,
       tageq_r, v0, v1, v2, v3, v4, v5, v6, v7, v8, v9, v10, v11, v12, v13, v14, v15, v_r, v_w, wd0, wd1,
       wd2, wd4, wd12, we2;
  wire [1:0] cnt0, cnt1, cnt2, cnt3, cnt4, cnt5, cnt6, cnt7, cnt8, cnt9, cnt10, cnt11, cnt12, cnt13, cnt14,
       cnt15, cnt_n, multiplexer_7_out;
  wire [3:0] caddr;
  wire [31:0] multiplexer_2_out, multiplexer_4_out, register_3_q, register_7_q, register_11_q, register_15_q,
       register_19_q, register_23_q, register_27_q, register_31_q, register_35_q, register_39_q,
       register_43_q, register_47_q, register_51_q, register_55_q, register_59_q, register_63_q, tag0, tgt1,
       tgt2, tgt3, tgt4, tgt5, tgt6, tgt7, tgt8, tgt9, tgt10, tgt11, tgt12, tgt13, tgt14, tgt15;

  Register #(.width(32)) register_1 (.D(wpc), .en(e0), .clk(clk), .Q(tag0));  // open: clr
  Decoder #(.select(4), .enable("false")) decoder_1 (
    .out0(wd0), .out1(wd1), .out2(wd2), .out3(decoder_1_out3), .out4(wd4), .out5(decoder_1_out5),
    .out6(decoder_1_out6), .out7(decoder_1_out7), .out8(decoder_1_out8), .out9(decoder_1_out9),
    .out10(decoder_1_out10), .out11(decoder_1_out11), .out12(wd12), .out13(decoder_1_out13),
    .out14(decoder_1_out14), .out15(decoder_1_out15), .sel(wpc[5:2]));
  and and_1 (and_1_out, we2, wd1);
  and and_2 (and_2_out, we2, wd2);
  and and_3 (and_3_out, we2, decoder_1_out3);
  and and_4 (and_4_out, we2, wd4);
  and and_5 (and_5_out, we2, decoder_1_out5);
  and and_6 (and_6_out, we2, decoder_1_out6);
  and and_7 (and_7_out, we2, decoder_1_out7);
  and and_8 (and_8_out, we2, decoder_1_out8);
  and and_9 (and_9_out, we2, decoder_1_out9);
  and and_10 (and_10_out, we2, decoder_1_out10);
  and and_11 (and_11_out, we2, decoder_1_out11);
  and and_12 (and_12_out, we2, wd12);
  and and_13 (and_13_out, we2, decoder_1_out13);
  and and_14 (and_14_out, we2, decoder_1_out14);
  and and_15 (and_15_out, we2, decoder_1_out15);
  Register #(.width(1)) register_2 (.D(1'b1), .en(and_1_out), .clk(clk), .Q(v1));  // open: clr
  Register #(.width(32)) register_3 (.D(wpc), .en(and_1_out), .clk(clk), .Q(register_3_q));  // open: clr
  Register #(.width(32)) register_4 (.D(wtgt), .en(and_1_out), .clk(clk), .Q(tgt1));  // open: clr
  Register #(.width(2)) register_5 (.D(cnt_n), .en(and_1_out), .clk(clk), .Q(cnt1));  // open: clr
  Register #(.width(1)) register_6 (.D(1'b1), .en(and_2_out), .clk(clk), .Q(v2));  // open: clr
  Register #(.width(32)) register_7 (.D(wpc), .en(and_2_out), .clk(clk), .Q(register_7_q));  // open: clr
  Register #(.width(32)) register_8 (.D(wtgt), .en(and_2_out), .clk(clk), .Q(tgt2));  // open: clr
  Register #(.width(2)) register_9 (.D(cnt_n), .en(and_2_out), .clk(clk), .Q(cnt2));  // open: clr
  Register #(.width(1)) register_10 (.D(1'b1), .en(and_3_out), .clk(clk), .Q(v3));  // open: clr
  Register #(.width(32)) register_11 (.D(wpc), .en(and_3_out), .clk(clk), .Q(register_11_q));  // open: clr
  Register #(.width(32)) register_12 (.D(wtgt), .en(and_3_out), .clk(clk), .Q(tgt3));  // open: clr
  Register #(.width(2)) register_13 (.D(cnt_n), .en(and_3_out), .clk(clk), .Q(cnt3));  // open: clr
  Register #(.width(1)) register_14 (.D(1'b1), .en(and_4_out), .clk(clk), .Q(v4));  // open: clr
  Register #(.width(32)) register_15 (.D(wpc), .en(and_4_out), .clk(clk), .Q(register_15_q));  // open: clr
  Register #(.width(32)) register_16 (.D(wtgt), .en(and_4_out), .clk(clk), .Q(tgt4));  // open: clr
  Register #(.width(2)) register_17 (.D(cnt_n), .en(and_4_out), .clk(clk), .Q(cnt4));  // open: clr
  Register #(.width(1)) register_18 (.D(1'b1), .en(and_5_out), .clk(clk), .Q(v5));  // open: clr
  Register #(.width(32)) register_19 (.D(wpc), .en(and_5_out), .clk(clk), .Q(register_19_q));  // open: clr
  Register #(.width(32)) register_20 (.D(wtgt), .en(and_5_out), .clk(clk), .Q(tgt5));  // open: clr
  Register #(.width(2)) register_21 (.D(cnt_n), .en(and_5_out), .clk(clk), .Q(cnt5));  // open: clr
  Register #(.width(1)) register_22 (.D(1'b1), .en(and_6_out), .clk(clk), .Q(v6));  // open: clr
  Register #(.width(32)) register_23 (.D(wpc), .en(and_6_out), .clk(clk), .Q(register_23_q));  // open: clr
  Register #(.width(32)) register_24 (.D(wtgt), .en(and_6_out), .clk(clk), .Q(tgt6));  // open: clr
  Register #(.width(2)) register_25 (.D(cnt_n), .en(and_6_out), .clk(clk), .Q(cnt6));  // open: clr
  Register #(.width(1)) register_26 (.D(1'b1), .en(and_7_out), .clk(clk), .Q(v7));  // open: clr
  Register #(.width(32)) register_27 (.D(wpc), .en(and_7_out), .clk(clk), .Q(register_27_q));  // open: clr
  Register #(.width(32)) register_28 (.D(wtgt), .en(and_7_out), .clk(clk), .Q(tgt7));  // open: clr
  Register #(.width(2)) register_29 (.D(cnt_n), .en(and_7_out), .clk(clk), .Q(cnt7));  // open: clr
  Register #(.width(1)) register_30 (.D(1'b1), .en(and_8_out), .clk(clk), .Q(v8));  // open: clr
  Register #(.width(32)) register_31 (.D(wpc), .en(and_8_out), .clk(clk), .Q(register_31_q));  // open: clr
  Register #(.width(32)) register_32 (.D(wtgt), .en(and_8_out), .clk(clk), .Q(tgt8));  // open: clr
  Register #(.width(2)) register_33 (.D(cnt_n), .en(and_8_out), .clk(clk), .Q(cnt8));  // open: clr
  Register #(.width(1)) register_34 (.D(1'b1), .en(and_9_out), .clk(clk), .Q(v9));  // open: clr
  Register #(.width(32)) register_35 (.D(wpc), .en(and_9_out), .clk(clk), .Q(register_35_q));  // open: clr
  Register #(.width(32)) register_36 (.D(wtgt), .en(and_9_out), .clk(clk), .Q(tgt9));  // open: clr
  Register #(.width(2)) register_37 (.D(cnt_n), .en(and_9_out), .clk(clk), .Q(cnt9));  // open: clr
  Register #(.width(1)) register_38 (.D(1'b1), .en(and_10_out), .clk(clk), .Q(v10));  // open: clr
  Register #(.width(32)) register_39 (.D(wpc), .en(and_10_out), .clk(clk), .Q(register_39_q));  // open: clr
  Register #(.width(32)) register_40 (.D(wtgt), .en(and_10_out), .clk(clk), .Q(tgt10));  // open: clr
  Register #(.width(2)) register_41 (.D(cnt_n), .en(and_10_out), .clk(clk), .Q(cnt10));  // open: clr
  Register #(.width(1)) register_42 (.D(1'b1), .en(and_11_out), .clk(clk), .Q(v11));  // open: clr
  Register #(.width(32)) register_43 (.D(wpc), .en(and_11_out), .clk(clk), .Q(register_43_q));  // open: clr
  Register #(.width(32)) register_44 (.D(wtgt), .en(and_11_out), .clk(clk), .Q(tgt11));  // open: clr
  Register #(.width(2)) register_45 (.D(cnt_n), .en(and_11_out), .clk(clk), .Q(cnt11));  // open: clr
  Register #(.width(1)) register_46 (.D(1'b1), .en(and_12_out), .clk(clk), .Q(v12));  // open: clr
  Register #(.width(32)) register_47 (.D(wpc), .en(and_12_out), .clk(clk), .Q(register_47_q));  // open: clr
  Register #(.width(32)) register_48 (.D(wtgt), .en(and_12_out), .clk(clk), .Q(tgt12));  // open: clr
  Register #(.width(2)) register_49 (.D(cnt_n), .en(and_12_out), .clk(clk), .Q(cnt12));  // open: clr
  Register #(.width(1)) register_50 (.D(1'b1), .en(and_13_out), .clk(clk), .Q(v13));  // open: clr
  Register #(.width(32)) register_51 (.D(wpc), .en(and_13_out), .clk(clk), .Q(register_51_q));  // open: clr
  Register #(.width(32)) register_52 (.D(wtgt), .en(and_13_out), .clk(clk), .Q(tgt13));  // open: clr
  Register #(.width(2)) register_53 (.D(cnt_n), .en(and_13_out), .clk(clk), .Q(cnt13));  // open: clr
  Register #(.width(1)) register_54 (.D(1'b1), .en(and_14_out), .clk(clk), .Q(v14));  // open: clr
  Register #(.width(32)) register_55 (.D(wpc), .en(and_14_out), .clk(clk), .Q(register_55_q));  // open: clr
  Register #(.width(32)) register_56 (.D(wtgt), .en(and_14_out), .clk(clk), .Q(tgt14));  // open: clr
  Register #(.width(2)) register_57 (.D(cnt_n), .en(and_14_out), .clk(clk), .Q(cnt14));  // open: clr
  Register #(.width(1)) register_58 (.D(1'b1), .en(and_15_out), .clk(clk), .Q(v15));  // open: clr
  Register #(.width(32)) register_59 (.D(wpc), .en(and_15_out), .clk(clk), .Q(register_59_q));  // open: clr
  Register #(.width(32)) register_60 (.D(wtgt), .en(and_15_out), .clk(clk), .Q(tgt15));  // open: clr
  Register #(.width(2)) register_61 (.D(cnt_n), .en(and_15_out), .clk(clk), .Q(cnt15));  // open: clr
  Multiplexer #(.width(1), .select(4)) multiplexer_1 (
    .in0(v0), .in1(v1), .in2(v2), .in3(v3), .in4(v4), .in5(v5), .in6(v6), .in7(v7), .in8(v8), .in9(v9),
    .in10(v10), .in11(v11), .in12(v12), .in13(v13), .in14(v14), .in15(v15), .out(v_w), .sel(wpc[5:2]));
  Multiplexer #(.width(32), .select(4)) multiplexer_2 (
    .in0(tag0), .in1(register_3_q), .in2(register_7_q), .in3(register_11_q), .in4(register_15_q),
    .in5(register_19_q), .in6(register_23_q), .in7(register_27_q), .in8(register_31_q), .in9(register_35_q),
    .in10(register_39_q), .in11(register_43_q), .in12(register_47_q), .in13(register_51_q),
    .in14(register_55_q), .in15(register_59_q), .out(multiplexer_2_out), .sel(wpc[5:2]));
  Multiplexer #(.width(2), .select(4)) multiplexer_3 (
    .in0(cnt0), .in1(cnt1), .in2(cnt2), .in3(cnt3), .in4(cnt4), .in5(cnt5), .in6(cnt6), .in7(cnt7),
    .in8(cnt8), .in9(cnt9), .in10(cnt10), .in11(cnt11), .in12(cnt12), .in13(cnt13), .in14(cnt14),
    .in15(cnt15), .out(caddr[1:0]), .sel(wpc[5:2]));
  Multiplexer #(.width(32), .select(4)) multiplexer_4 (
    .in0(tag0), .in1(register_3_q), .in2(register_7_q), .in3(register_11_q), .in4(register_15_q),
    .in5(register_19_q), .in6(register_23_q), .in7(register_27_q), .in8(register_31_q), .in9(register_35_q),
    .in10(register_39_q), .in11(register_43_q), .in12(register_47_q), .in13(register_51_q),
    .in14(register_55_q), .in15(register_59_q), .out(multiplexer_4_out), .sel(rpc[5:2]));
  Comparator #(.width(32), .mode("unsigned")) comparator_1 (
    .a(multiplexer_2_out), .b(wpc), .eq(comparator_1_eq));  // open: gt, lt
  Comparator #(.width(32), .mode("unsigned")) comparator_2 (
    .a(multiplexer_4_out), .b(rpc), .eq(tageq_r));  // open: gt, lt
  and and_16 (caddr[3], v_w, comparator_1_eq);
  or or_1 (or_1_out, caddr[3], wtk);
  ROM #(.addrWidth(4), .dataWidth(2)) CNT_NEXT (.addr({caddr[3], wtk, caddr[1:0]}), .data(cnt_n));
  and and_17 (we2, we, or_1_out);
  and and_18 (e0, we2, wd0);
  Register #(.width(1)) register_62 (.D(1'b1), .en(e0), .clk(clk), .Q(v0));  // open: clr
  Register #(.width(32)) register_63 (.D(wtgt), .en(e0), .clk(clk), .Q(register_63_q));  // open: clr
  Register #(.width(2)) register_64 (.D(cnt_n), .en(e0), .clk(clk), .Q(cnt0));  // open: clr
  Multiplexer #(.width(1), .select(4)) multiplexer_5 (
    .in0(v0), .in1(v1), .in2(v2), .in3(v3), .in4(v4), .in5(v5), .in6(v6), .in7(v7), .in8(v8), .in9(v9),
    .in10(v10), .in11(v11), .in12(v12), .in13(v13), .in14(v14), .in15(v15), .out(v_r), .sel(rpc[5:2]));
  Multiplexer #(.width(32), .select(4)) multiplexer_6 (
    .in0(register_63_q), .in1(tgt1), .in2(tgt2), .in3(tgt3), .in4(tgt4), .in5(tgt5), .in6(tgt6), .in7(tgt7),
    .in8(tgt8), .in9(tgt9), .in10(tgt10), .in11(tgt11), .in12(tgt12), .in13(tgt13), .in14(tgt14),
    .in15(tgt15), .out(ptgt), .sel(rpc[5:2]));
  Multiplexer #(.width(2), .select(4)) multiplexer_7 (
    .in0(cnt0), .in1(cnt1), .in2(cnt2), .in3(cnt3), .in4(cnt4), .in5(cnt5), .in6(cnt6), .in7(cnt7),
    .in8(cnt8), .in9(cnt9), .in10(cnt10), .in11(cnt11), .in12(cnt12), .in13(cnt13), .in14(cnt14),
    .in15(cnt15), .out(multiplexer_7_out), .sel(rpc[5:2]));
  and and_19 (ptk, v_r, tageq_r, multiplexer_7_out[1]);

  // Other names for the same wires on the sheet: cnt_w[1:0] = caddr[1:0]; caddr[2] = wtk; present = caddr[3];
  //   ri[3:0] = rpc[5:2]; wi[3:0] = wpc[5:2]

  // Notes on the sheet:
  //   contents of CNT_NEXT (hex, n*v repeats v):
  //   1 1 1 1 2 2 2 2 0 0 1 2 1 2 3 3
endmodule

module DCache (
  input  clk,
  input  [9:0] addr,
  input  wr,
  input  [31:0] wdata,
  input  [31:0] mdata,
  input  fill,
  output hit,
  output [31:0] data
);

  wire and_1_out, and_2_out, and_3_out, and_4_out, and_5_out, and_6_out, and_7_out, and_8_out, and_9_out,
       and_10_out, and_11_out, and_12_out, and_13_out, and_14_out, and_15_out, and_16_out, comparator_1_eq,
       d0, d1, d4, d12, decoder_1_out2, decoder_1_out3, decoder_1_out5, decoder_1_out6, decoder_1_out7,
       decoder_1_out8, decoder_1_out9, decoder_1_out10, decoder_1_out11, decoder_1_out13, decoder_1_out14,
       decoder_1_out15, lwe, register_10_q, register_13_q, register_16_q, register_19_q, register_22_q,
       register_25_q, register_28_q, register_31_q, register_34_q, register_37_q, register_40_q,
       register_46_q, v0, v1, v2, v14, v_r;
  wire [5:0] multiplexer_3_out, register_11_q, register_14_q, register_17_q, register_20_q, register_23_q,
       register_26_q, register_29_q, register_32_q, register_35_q, register_38_q, register_41_q,
       register_47_q, t0, t1, t2, t14;
  wire [31:0] l0, l1, l2, l14, ld, register_12_q, register_15_q, register_18_q, register_21_q, register_24_q,
       register_27_q, register_30_q, register_33_q, register_36_q, register_39_q, register_42_q,
       register_48_q;

  or or_1 (lwe, wr, fill);
  Multiplexer #(.width(32), .select(1)) multiplexer_1 (.in0(mdata), .in1(wdata), .out(ld), .sel(wr));
  Decoder #(.select(4), .enable("false")) decoder_1 (
    .out0(d0), .out1(d1), .out2(decoder_1_out2), .out3(decoder_1_out3), .out4(d4), .out5(decoder_1_out5),
    .out6(decoder_1_out6), .out7(decoder_1_out7), .out8(decoder_1_out8), .out9(decoder_1_out9),
    .out10(decoder_1_out10), .out11(decoder_1_out11), .out12(d12), .out13(decoder_1_out13),
    .out14(decoder_1_out14), .out15(decoder_1_out15), .sel(addr[3:0]));
  and and_1 (and_1_out, lwe, d0);
  and and_2 (and_2_out, lwe, d1);
  and and_3 (and_3_out, lwe, decoder_1_out2);
  and and_4 (and_4_out, lwe, decoder_1_out3);
  and and_5 (and_5_out, lwe, d4);
  and and_6 (and_6_out, lwe, decoder_1_out5);
  and and_7 (and_7_out, lwe, decoder_1_out6);
  and and_8 (and_8_out, lwe, decoder_1_out7);
  and and_9 (and_9_out, lwe, decoder_1_out8);
  and and_10 (and_10_out, lwe, decoder_1_out9);
  and and_11 (and_11_out, lwe, decoder_1_out10);
  and and_12 (and_12_out, lwe, decoder_1_out11);
  and and_13 (and_13_out, lwe, d12);
  and and_14 (and_14_out, lwe, decoder_1_out13);
  and and_15 (and_15_out, lwe, decoder_1_out14);
  and and_16 (and_16_out, lwe, decoder_1_out15);
  Register #(.width(1)) register_1 (.D(1'b1), .en(and_1_out), .clk(clk), .Q(v0));  // open: clr
  Register #(.width(6)) register_2 (.D(addr[9:4]), .en(and_1_out), .clk(clk), .Q(t0));  // open: clr
  Register #(.width(32)) register_3 (.D(ld), .en(and_1_out), .clk(clk), .Q(l0));  // open: clr
  Register #(.width(1)) register_4 (.D(1'b1), .en(and_2_out), .clk(clk), .Q(v1));  // open: clr
  Register #(.width(6)) register_5 (.D(addr[9:4]), .en(and_2_out), .clk(clk), .Q(t1));  // open: clr
  Register #(.width(32)) register_6 (.D(ld), .en(and_2_out), .clk(clk), .Q(l1));  // open: clr
  Register #(.width(1)) register_7 (.D(1'b1), .en(and_3_out), .clk(clk), .Q(v2));  // open: clr
  Register #(.width(6)) register_8 (.D(addr[9:4]), .en(and_3_out), .clk(clk), .Q(t2));  // open: clr
  Register #(.width(32)) register_9 (.D(ld), .en(and_3_out), .clk(clk), .Q(l2));  // open: clr
  Register #(.width(1)) register_10 (.D(1'b1), .en(and_4_out), .clk(clk), .Q(register_10_q));  // open: clr
  Register #(.width(6)) register_11 (.D(addr[9:4]), .en(and_4_out), .clk(clk), .Q(register_11_q));  // open: clr
  Register #(.width(32)) register_12 (.D(ld), .en(and_4_out), .clk(clk), .Q(register_12_q));  // open: clr
  Register #(.width(1)) register_13 (.D(1'b1), .en(and_5_out), .clk(clk), .Q(register_13_q));  // open: clr
  Register #(.width(6)) register_14 (.D(addr[9:4]), .en(and_5_out), .clk(clk), .Q(register_14_q));  // open: clr
  Register #(.width(32)) register_15 (.D(ld), .en(and_5_out), .clk(clk), .Q(register_15_q));  // open: clr
  Register #(.width(1)) register_16 (.D(1'b1), .en(and_6_out), .clk(clk), .Q(register_16_q));  // open: clr
  Register #(.width(6)) register_17 (.D(addr[9:4]), .en(and_6_out), .clk(clk), .Q(register_17_q));  // open: clr
  Register #(.width(32)) register_18 (.D(ld), .en(and_6_out), .clk(clk), .Q(register_18_q));  // open: clr
  Register #(.width(1)) register_19 (.D(1'b1), .en(and_7_out), .clk(clk), .Q(register_19_q));  // open: clr
  Register #(.width(6)) register_20 (.D(addr[9:4]), .en(and_7_out), .clk(clk), .Q(register_20_q));  // open: clr
  Register #(.width(32)) register_21 (.D(ld), .en(and_7_out), .clk(clk), .Q(register_21_q));  // open: clr
  Register #(.width(1)) register_22 (.D(1'b1), .en(and_8_out), .clk(clk), .Q(register_22_q));  // open: clr
  Register #(.width(6)) register_23 (.D(addr[9:4]), .en(and_8_out), .clk(clk), .Q(register_23_q));  // open: clr
  Register #(.width(32)) register_24 (.D(ld), .en(and_8_out), .clk(clk), .Q(register_24_q));  // open: clr
  Register #(.width(1)) register_25 (.D(1'b1), .en(and_9_out), .clk(clk), .Q(register_25_q));  // open: clr
  Register #(.width(6)) register_26 (.D(addr[9:4]), .en(and_9_out), .clk(clk), .Q(register_26_q));  // open: clr
  Register #(.width(32)) register_27 (.D(ld), .en(and_9_out), .clk(clk), .Q(register_27_q));  // open: clr
  Register #(.width(1)) register_28 (.D(1'b1), .en(and_10_out), .clk(clk), .Q(register_28_q));  // open: clr
  Register #(.width(6)) register_29 (.D(addr[9:4]), .en(and_10_out), .clk(clk), .Q(register_29_q));  // open: clr
  Register #(.width(32)) register_30 (.D(ld), .en(and_10_out), .clk(clk), .Q(register_30_q));  // open: clr
  Register #(.width(1)) register_31 (.D(1'b1), .en(and_11_out), .clk(clk), .Q(register_31_q));  // open: clr
  Register #(.width(6)) register_32 (.D(addr[9:4]), .en(and_11_out), .clk(clk), .Q(register_32_q));  // open: clr
  Register #(.width(32)) register_33 (.D(ld), .en(and_11_out), .clk(clk), .Q(register_33_q));  // open: clr
  Register #(.width(1)) register_34 (.D(1'b1), .en(and_12_out), .clk(clk), .Q(register_34_q));  // open: clr
  Register #(.width(6)) register_35 (.D(addr[9:4]), .en(and_12_out), .clk(clk), .Q(register_35_q));  // open: clr
  Register #(.width(32)) register_36 (.D(ld), .en(and_12_out), .clk(clk), .Q(register_36_q));  // open: clr
  Register #(.width(1)) register_37 (.D(1'b1), .en(and_13_out), .clk(clk), .Q(register_37_q));  // open: clr
  Register #(.width(6)) register_38 (.D(addr[9:4]), .en(and_13_out), .clk(clk), .Q(register_38_q));  // open: clr
  Register #(.width(32)) register_39 (.D(ld), .en(and_13_out), .clk(clk), .Q(register_39_q));  // open: clr
  Register #(.width(1)) register_40 (.D(1'b1), .en(and_14_out), .clk(clk), .Q(register_40_q));  // open: clr
  Register #(.width(6)) register_41 (.D(addr[9:4]), .en(and_14_out), .clk(clk), .Q(register_41_q));  // open: clr
  Register #(.width(32)) register_42 (.D(ld), .en(and_14_out), .clk(clk), .Q(register_42_q));  // open: clr
  Register #(.width(1)) register_43 (.D(1'b1), .en(and_15_out), .clk(clk), .Q(v14));  // open: clr
  Register #(.width(6)) register_44 (.D(addr[9:4]), .en(and_15_out), .clk(clk), .Q(t14));  // open: clr
  Register #(.width(32)) register_45 (.D(ld), .en(and_15_out), .clk(clk), .Q(l14));  // open: clr
  Register #(.width(1)) register_46 (.D(1'b1), .en(and_16_out), .clk(clk), .Q(register_46_q));  // open: clr
  Register #(.width(6)) register_47 (.D(addr[9:4]), .en(and_16_out), .clk(clk), .Q(register_47_q));  // open: clr
  Register #(.width(32)) register_48 (.D(ld), .en(and_16_out), .clk(clk), .Q(register_48_q));  // open: clr
  Multiplexer #(.width(1), .select(4)) multiplexer_2 (
    .in0(v0), .in1(v1), .in2(v2), .in3(register_10_q), .in4(register_13_q), .in5(register_16_q),
    .in6(register_19_q), .in7(register_22_q), .in8(register_25_q), .in9(register_28_q), .in10(register_31_q),
    .in11(register_34_q), .in12(register_37_q), .in13(register_40_q), .in14(v14), .in15(register_46_q),
    .out(v_r), .sel(addr[3:0]));
  Multiplexer #(.width(6), .select(4)) multiplexer_3 (
    .in0(t0), .in1(t1), .in2(t2), .in3(register_11_q), .in4(register_14_q), .in5(register_17_q),
    .in6(register_20_q), .in7(register_23_q), .in8(register_26_q), .in9(register_29_q), .in10(register_32_q),
    .in11(register_35_q), .in12(register_38_q), .in13(register_41_q), .in14(t14), .in15(register_47_q),
    .out(multiplexer_3_out), .sel(addr[3:0]));
  Multiplexer #(.width(32), .select(4)) multiplexer_4 (
    .in0(l0), .in1(l1), .in2(l2), .in3(register_12_q), .in4(register_15_q), .in5(register_18_q),
    .in6(register_21_q), .in7(register_24_q), .in8(register_27_q), .in9(register_30_q), .in10(register_33_q),
    .in11(register_36_q), .in12(register_39_q), .in13(register_42_q), .in14(l14), .in15(register_48_q),
    .out(data), .sel(addr[3:0]));
  Comparator #(.width(6), .mode("unsigned")) comparator_1 (
    .a(multiplexer_3_out), .b(addr[9:4]), .eq(comparator_1_eq));  // open: gt, lt
  and and_17 (hit, v_r, comparator_1_eq);

  // Other names for the same wires on the sheet: idx[3:0] = addr[3:0]; tag[5:0] = addr[9:4]
endmodule

module CSRFile (
  input  clk,
  input  en,
  input  we,
  input  [11:0] addr,
  input  [2:0] f3,
  input  [31:0] rs1v,
  input  [4:0] zimm,
  input  mret,
  input  trap,
  input  [31:0] epc,
  input  msip,
  input  mtip,
  input  meip,
  input  [31:0] cycles,
  output [31:0] rdata,
  output [31:0] mtvec,
  output [31:0] mepc,
  output irq,
  output [31:0] cause
);

  wire and_2_out, and_6_out, and_7_out, and_16_out, comparator_1_eq, comparator_2_eq, comparator_3_eq,
       comparator_4_eq, comparator_5_eq, comparator_6_eq, comparator_7_eq, comparator_8_eq, comparator_9_eq,
       e_cause, e_epc, e_ms, MEIE, MIE, MPIE, mret_g, MSIE, MTIE, multiplexer_4_out, multiplexer_5_out,
       multiplexer_7_out, multiplexer_10_out, n3, n11, not_1_out, or_1_out, pany, pe_e, pe_s, w_mie,
       w_mscratch, w_mtvec, wen;
  wire [31:0] and_11_out, and_21_out, bit_extender_7_out, bit_extender_8_out, d_mepc, g_cycles, g_mcause,
       g_mepc, g_mscratch, g_mtvec, g_v_mie, g_v_mip, m_mcause, m_mepc, m_mscratch, m_mtvec, m_v_mie,
       m_v_mstatus, multiplexer_6_out, multiplexer_9_out, \new , not_2_out, register_2_q, register_8_q, src,
       vor;

  Comparator #(.width(12), .mode("unsigned")) comparator_1 (
    .a(addr), .b(12'h300), .eq(comparator_1_eq));  // open: gt, lt
  Comparator #(.width(12), .mode("unsigned")) comparator_2 (
    .a(addr), .b(12'h304), .eq(comparator_2_eq));  // open: gt, lt
  Comparator #(.width(12), .mode("unsigned")) comparator_3 (
    .a(addr), .b(12'h305), .eq(comparator_3_eq));  // open: gt, lt
  Comparator #(.width(12), .mode("unsigned")) comparator_4 (
    .a(addr), .b(12'h340), .eq(comparator_4_eq));  // open: gt, lt
  Comparator #(.width(12), .mode("unsigned")) comparator_5 (
    .a(addr), .b(12'h341), .eq(comparator_5_eq));  // open: gt, lt
  Comparator #(.width(12), .mode("unsigned")) comparator_6 (
    .a(addr), .b(12'h342), .eq(comparator_6_eq));  // open: gt, lt
  Comparator #(.width(12), .mode("unsigned")) comparator_7 (
    .a(addr), .b(12'h344), .eq(comparator_7_eq));  // open: gt, lt
  Comparator #(.width(12), .mode("unsigned")) comparator_8 (
    .a(addr), .b(12'hc00), .eq(comparator_8_eq));  // open: gt, lt
  Comparator #(.width(12), .mode("unsigned")) comparator_9 (
    .a(addr), .b(12'hb00), .eq(comparator_9_eq));  // open: gt, lt
  and and_1 (wen, we, en);
  not not_1 (not_1_out, trap);
  or or_1 (or_1_out, comparator_8_eq, comparator_9_eq);
  assign m_v_mstatus = {{31{comparator_1_eq}}, comparator_1_eq};  // Bit_Extender bit_extender_1
  assign m_v_mie = {{31{comparator_2_eq}}, comparator_2_eq};  // Bit_Extender bit_extender_2
  assign m_mtvec = {{31{comparator_3_eq}}, comparator_3_eq};  // Bit_Extender bit_extender_3
  assign m_mscratch = {{31{comparator_4_eq}}, comparator_4_eq};  // Bit_Extender bit_extender_4
  assign m_mepc = {{31{comparator_5_eq}}, comparator_5_eq};  // Bit_Extender bit_extender_5
  assign m_mcause = {{31{comparator_6_eq}}, comparator_6_eq};  // Bit_Extender bit_extender_6
  assign bit_extender_7_out = {{31{comparator_7_eq}}, comparator_7_eq};  // Bit_Extender bit_extender_7
  Multiplexer #(.width(32), .select(1)) multiplexer_1 (.in0(rs1v), .in1({{27{1'b0}}, zimm}), .out(src), .sel(f3[2]));
  and and_2 (and_2_out, wen, comparator_1_eq);
  and and_3 (w_mie, wen, comparator_2_eq);
  and and_4 (w_mtvec, wen, comparator_3_eq);
  and and_5 (w_mscratch, wen, comparator_4_eq);
  and and_6 (and_6_out, wen, comparator_5_eq);
  and and_7 (and_7_out, wen, comparator_6_eq);
  and and_8 (mret_g, mret, en, not_1_out);
  assign g_v_mip = {{20{1'b0}}, meip, 3'b000, mtip, 3'b000, msip, 3'b000} & bit_extender_7_out;  // AND_Gate and_9, 32 bits wide
  assign bit_extender_8_out = {{31{or_1_out}}, or_1_out};  // Bit_Extender bit_extender_8
  assign vor = rdata | src;  // OR_Gate or_2, 32 bits wide
  assign not_2_out = ~src;  // NOT_Gate not_2, 32 bits wide
  or or_3 (e_epc, and_6_out, trap);
  or or_4 (e_cause, and_7_out, trap);
  or or_5 (e_ms, and_2_out, mret_g, trap);
  assign g_cycles = cycles & bit_extender_8_out;  // AND_Gate and_10, 32 bits wide
  assign and_11_out = rdata & not_2_out;  // AND_Gate and_11, 32 bits wide
  Multiplexer #(.width(32), .select(2)) multiplexer_2 (
    .in0(rdata), .in1(src), .in2(vor), .in3(and_11_out),
    .out({\new [31:12], n11, \new [10:4], n3, \new [2:0]}), .sel(f3[1:0]));
  Register #(.width(32)) register_1 (
    .D({\new [31:12], n11, \new [10:4], n3, \new [2:0]}), .en(w_mtvec), .clk(clk), .Q(mtvec));  // open: clr
  Register #(.width(32)) register_2 (
    .D({\new [31:12], n11, \new [10:4], n3, \new [2:0]}), .en(w_mscratch), .clk(clk), .Q(register_2_q));  // open: clr
  Multiplexer #(.width(32), .select(1)) multiplexer_3 (
    .in0({\new [31:12], n11, \new [10:4], n3, \new [2:0]}), .in1(epc), .out(d_mepc), .sel(trap));
  Register #(.width(1)) register_3 (.D(n3), .en(w_mie), .clk(clk), .Q(MSIE));  // open: clr
  Register #(.width(1)) register_4 (.D(\new [7]), .en(w_mie), .clk(clk), .Q(MTIE));  // open: clr
  Register #(.width(1)) register_5 (.D(n11), .en(w_mie), .clk(clk), .Q(MEIE));  // open: clr
  Register #(.width(32)) register_6 (.D(d_mepc), .en(e_epc), .clk(clk), .Q(mepc));  // open: clr
  assign g_mtvec = mtvec & m_mtvec;  // AND_Gate and_12, 32 bits wide
  assign g_mscratch = register_2_q & m_mscratch;  // AND_Gate and_13, 32 bits wide
  Multiplexer #(.width(1), .select(1)) multiplexer_4 (
    .in0(\new [7]), .in1(1'b1), .out(multiplexer_4_out), .sel(mret_g));
  Multiplexer #(.width(1), .select(1)) multiplexer_5 (
    .in0(multiplexer_4_out), .in1(MIE), .out(multiplexer_5_out), .sel(trap));
  assign g_mepc = mepc & m_mepc;  // AND_Gate and_14, 32 bits wide
  and and_15 (pe_s, msip, MSIE);
  and and_16 (and_16_out, mtip, MTIE);
  and and_17 (pe_e, meip, MEIE);
  Register #(.width(1)) register_7 (.D(multiplexer_5_out), .en(e_ms), .clk(clk), .Q(MPIE));  // open: clr
  assign g_v_mie = {{20{1'b0}}, MEIE, 3'b000, MTIE, 3'b000, MSIE, 3'b000} & m_v_mie;  // AND_Gate and_18, 32 bits wide
  or or_6 (pany, pe_s, and_16_out, pe_e);
  Multiplexer #(.width(32), .select(1)) multiplexer_6 (
    .in0(32'h80000007), .in1(32'h80000003), .out(multiplexer_6_out), .sel(pe_s));
  Multiplexer #(.width(1), .select(1)) multiplexer_7 (.in0(n3), .in1(MPIE), .out(multiplexer_7_out), .sel(mret_g));
  Multiplexer #(.width(32), .select(1)) multiplexer_8 (
    .in0(multiplexer_6_out), .in1(32'h8000000b), .out(cause), .sel(pe_e));
  Multiplexer #(.width(32), .select(1)) multiplexer_9 (
    .in0({\new [31:12], n11, \new [10:4], n3, \new [2:0]}), .in1(cause), .out(multiplexer_9_out), .sel(trap));
  Multiplexer #(.width(1), .select(1)) multiplexer_10 (
    .in0(multiplexer_7_out), .in1(1'b0), .out(multiplexer_10_out), .sel(trap));
  Register #(.width(32)) register_8 (.D(multiplexer_9_out), .en(e_cause), .clk(clk), .Q(register_8_q));  // open: clr
  Register #(.width(1)) register_9 (.D(multiplexer_10_out), .en(e_ms), .clk(clk), .Q(MIE));  // open: clr
  assign g_mcause = register_8_q & m_mcause;  // AND_Gate and_19, 32 bits wide
  and and_20 (irq, MIE, pany);
  assign and_21_out = {24'h18, MPIE, 3'b000, MIE, 3'b000} & m_v_mstatus;  // AND_Gate and_21, 32 bits wide
  assign rdata = and_21_out | g_v_mie | g_mtvec | g_mscratch | g_mepc | g_mcause | g_v_mip | g_cycles;  // OR_Gate or_7, 32 bits wide

  // Other names for the same wires on the sheet: cop[1:0] = f3[1:0]; isimm = f3[2]; new (some bits) = {n11, n3};
  //   v_mie (some bits) = {MEIE, MTIE, MSIE}; v_mip (some bits) = {meip, mtip, msip};
  //   v_mstatus (some bits) = {MPIE, MIE}; zx[4:0] = zimm
endmodule

module MMIO (
  input  clk,
  input  [31:0] addr,
  input  we,
  input  [31:0] wdata,
  input  [7:0] sw,
  input  [31:0] cycles,
  output [31:0] rdata,
  output isio,
  output [7:0] led,
  output msip,
  output mtip,
  output tx_we,
  output [6:0] tx_d
);

  wire and_2_out, and_4_out, and_5_out, comparator_1_lt, decoder_1_out2, decoder_1_out5, s0, s4, wio;
  wire [31:0] bit_extender_2_out, bit_extender_3_out, ncmp_d, not_2_out, r_sw, register_3_q;

  assign ncmp_d = ~wdata;  // NOT_Gate not_1, 32 bits wide
  assign r_sw = {{24{1'b0}}, sw};  // Bit_Extender bit_extender_1
  Decoder #(.select(3), .enable("false")) decoder_1 (
    .out0(s0), .out2(decoder_1_out2), .out4(s4), .out5(decoder_1_out5), .sel(addr[4:2]));  // open: out1, out3, out6, out7
  and and_1 (wio, we, addr[31]);
  and and_2 (and_2_out, wio, s0);
  and and_3 (tx_we, wio, decoder_1_out2);
  and and_4 (and_4_out, wio, s4);
  and and_5 (and_5_out, wio, decoder_1_out5);
  Register #(.width(8)) register_1 (.D(wdata[7:0]), .en(and_2_out), .clk(clk), .Q(led));  // open: clr
  Register #(.width(1)) register_2 (.D(wdata[0]), .en(and_4_out), .clk(clk), .Q(msip));  // open: clr
  Register #(.width(32)) register_3 (.D(ncmp_d), .en(and_5_out), .clk(clk), .Q(register_3_q));  // open: clr
  assign not_2_out = ~register_3_q;  // NOT_Gate not_2, 32 bits wide
  assign bit_extender_2_out = {{24{1'b0}}, led};  // Bit_Extender bit_extender_2
  assign bit_extender_3_out = {{31{1'b0}}, msip};  // Bit_Extender bit_extender_3
  Comparator #(.width(32), .mode("unsigned")) comparator_1 (
    .a(cycles), .b(not_2_out), .lt(comparator_1_lt));  // open: gt, eq
  Multiplexer #(.width(32), .select(3)) multiplexer_1 (
    .in0(bit_extender_2_out), .in1(r_sw), .in2({32{1'b0}}), .in3(32'h1), .in4(bit_extender_3_out),
    .in5(not_2_out), .in6(cycles), .in7({32{1'b0}}), .out(rdata), .sel(addr[4:2]));
  not not_3 (mtip, comparator_1_lt);

  assign isio = addr[31];
  assign tx_d = wdata[6:0];

  // Other names for the same wires on the sheet: sel[2:0] = addr[4:2]; wd0 = wdata[0]; wd8[7:0] = wdata[7:0]
endmodule

module IF_ID (
  input  clk,
  input  [31:0] f_instr_q,
  input  f_pt_q,
  input  [31:0] f_ptgt,
  input  [31:0] pc,
  input  pcen,
  output [31:0] d_instr,
  output [31:0] d_pc,
  output d_pt,
  output [31:0] d_ptgt
);

  Register #(.width(32)) register_1 (.D(pc), .en(pcen), .clk(clk), .Q(d_pc));  // open: clr
  Register #(.width(32)) register_2 (.D(f_instr_q), .en(pcen), .clk(clk), .Q(d_instr));  // open: clr
  Register #(.width(1)) register_3 (.D(f_pt_q), .en(pcen), .clk(clk), .Q(d_pt));  // open: clr
  Register #(.width(32)) register_4 (.D(f_ptgt), .en(pcen), .clk(clk), .Q(d_ptgt));  // open: clr
endmodule

module InstrDecode (
  input  d_RdF,
  input  d_Rs1F,
  input  d_Rs2F,
  input  [31:0] d_instr,
  output [2:0] d_f3,
  output [5:0] d_rd,
  output [5:0] d_rs1,
  output [5:0] d_rs2
);


  assign d_f3 = d_instr[14:12];
  assign d_rd = {d_RdF, d_instr[11:7]};
  assign d_rs1 = {d_Rs1F, d_instr[19:15]};
  assign d_rs2 = {d_Rs2F, d_instr[24:20]};

  // Other names for the same wires on the sheet: d_rdx[4:0] = d_instr[11:7]; d_rs1x[4:0] = d_instr[19:15];
  //   d_rs2x[4:0] = d_instr[24:20]
endmodule

module MainControl (
  input  [31:0] d_instr,
  output [2:0] d_ImmSel,
  output d_MemWrite,
  output d_RdF,
  output d_Rs1F,
  output d_Rs2F,
  output d_UseRs1,
  output d_UseRs2,
  output [31:0] d_ctrl
);

  Control control_1 (.instr(d_instr), .ctrl(d_ctrl));

  assign d_ImmSel = d_ctrl[15:13];
  assign d_MemWrite = d_ctrl[9];
  assign d_RdF = d_ctrl[29];
  assign d_Rs1F = d_ctrl[30];
  assign d_Rs2F = d_ctrl[31];
  assign d_UseRs1 = d_ctrl[20];
  assign d_UseRs2 = d_ctrl[21];
endmodule

module HazardUnit (
  input  d_MemWrite,
  input  d_UseRs1,
  input  d_UseRs2,
  input  [31:0] d_ctrl,
  input  d_pt,
  input  [5:0] d_rs1,
  input  [5:0] d_rs2,
  input  e_MemRead,
  input  [5:0] e_rd,
  input  e_rdnz,
  input  nmstall,
  input  redir,
  output [31:0] d_ctrl_q,
  output d_pt_q,
  output pcen,
  output stall
);

  wire and_1_out, and_2_out, bubble, comparator_1_eq, comparator_2_eq, not_1_out, not_2_out, or_1_out,
       or_3_out;

  Comparator #(.width(6), .mode("unsigned")) comparator_1 (.a(e_rd), .b(d_rs1), .eq(comparator_1_eq));  // open: gt, lt
  Comparator #(.width(6), .mode("unsigned")) comparator_2 (.a(e_rd), .b(d_rs2), .eq(comparator_2_eq));  // open: gt, lt
  not not_1 (not_1_out, d_MemWrite);
  and and_1 (and_1_out, comparator_1_eq, d_UseRs1);
  and and_2 (and_2_out, comparator_2_eq, d_UseRs2, not_1_out);
  or or_1 (or_1_out, and_1_out, and_2_out);
  and and_3 (stall, e_MemRead, e_rdnz, or_1_out);
  not not_2 (not_2_out, stall);
  or or_2 (bubble, stall, redir);
  Multiplexer #(.width(32), .select(1)) multiplexer_1 (.in0(d_ctrl), .in1({32{1'b0}}), .out(d_ctrl_q), .sel(bubble));
  Multiplexer #(.width(1), .select(1)) multiplexer_2 (.in0(d_pt), .in1(1'b0), .out(d_pt_q), .sel(bubble));
  or or_3 (or_3_out, not_2_out, redir);
  and and_4 (pcen, or_3_out, nmstall);
endmodule

module ForwardUnit (
  input  [5:0] d_rs1,
  input  [5:0] d_rs2,
  input  [5:0] e_rd,
  input  [5:0] e_rs1,
  input  [5:0] e_rs2,
  input  m_RegWrite,
  input  [5:0] m_rd,
  input  w_RegWrite,
  input  [5:0] w_rd,
  output e_rdnz,
  output fm1,
  output fm2,
  output fw1,
  output fw2,
  output w_rdnz,
  output wb_byp1,
  output wb_byp2
);

  wire comparator_1_eq, comparator_2_eq, comparator_3_eq, fm_eq1, fm_eq2, fw_eq1, fw_eq2, not_2_out, wb_eq1,
       wb_eq2;

  Comparator #(.width(6), .mode("unsigned")) comparator_1 (
    .a(w_rd), .b({6{1'b0}}), .eq(comparator_1_eq));  // open: gt, lt
  Comparator #(.width(6), .mode("unsigned")) comparator_2 (
    .a(m_rd), .b({6{1'b0}}), .eq(comparator_2_eq));  // open: gt, lt
  Comparator #(.width(6), .mode("unsigned")) comparator_3 (
    .a(e_rd), .b({6{1'b0}}), .eq(comparator_3_eq));  // open: gt, lt
  Comparator #(.width(6), .mode("unsigned")) comparator_4 (.a(w_rd), .b(d_rs1), .eq(wb_eq1));  // open: gt, lt
  Comparator #(.width(6), .mode("unsigned")) comparator_5 (.a(m_rd), .b(e_rs1), .eq(fm_eq1));  // open: gt, lt
  Comparator #(.width(6), .mode("unsigned")) comparator_6 (.a(w_rd), .b(e_rs1), .eq(fw_eq1));  // open: gt, lt
  Comparator #(.width(6), .mode("unsigned")) comparator_7 (.a(w_rd), .b(d_rs2), .eq(wb_eq2));  // open: gt, lt
  Comparator #(.width(6), .mode("unsigned")) comparator_8 (.a(m_rd), .b(e_rs2), .eq(fm_eq2));  // open: gt, lt
  Comparator #(.width(6), .mode("unsigned")) comparator_9 (.a(w_rd), .b(e_rs2), .eq(fw_eq2));  // open: gt, lt
  not not_1 (w_rdnz, comparator_1_eq);
  not not_2 (not_2_out, comparator_2_eq);
  not not_3 (e_rdnz, comparator_3_eq);
  and and_1 (wb_byp1, wb_eq1, w_RegWrite, w_rdnz);
  and and_2 (fm1, fm_eq1, m_RegWrite, not_2_out);
  and and_3 (fw1, fw_eq1, w_RegWrite, w_rdnz);
  and and_4 (wb_byp2, wb_eq2, w_RegWrite, w_rdnz);
  and and_5 (fm2, fm_eq2, m_RegWrite, not_2_out);
  and and_6 (fw2, fw_eq2, w_RegWrite, w_rdnz);
endmodule

module ID_EX (
  input  clk,
  input  [31:0] d_ctrl_q,
  input  [2:0] d_f3,
  input  [31:0] d_imm,
  input  [31:0] d_pc,
  input  d_pt_q,
  input  [31:0] d_ptgt,
  input  [31:0] d_r1,
  input  [31:0] d_r2,
  input  [5:0] d_rd,
  input  [5:0] d_rs1,
  input  [5:0] d_rs2,
  input  nmstall,
  output [3:0] e_ALUOp,
  output [1:0] e_ASel,
  output e_BSel,
  output e_Branch,
  output e_Csr,
  output [3:0] e_FpOp,
  output e_Jal,
  output e_Jalr,
  output e_MemRead,
  output e_Mret,
  output [2:0] e_ResSel,
  output e_Valid,
  output [31:0] e_ctrl,
  output [2:0] e_f3,
  output [31:0] e_imm,
  output [31:0] e_pc,
  output e_pt,
  output [31:0] e_ptgt,
  output [31:0] e_r1,
  output [31:0] e_r2,
  output [5:0] e_rd,
  output [5:0] e_rs1,
  output [5:0] e_rs2
);

  Register #(.width(32)) register_1 (
    .D(d_ctrl_q), .en(nmstall), .clk(clk),
    .Q({e_ctrl[31:24], e_Csr, e_ctrl[22:17], e_Branch, e_ctrl[15:8], e_ALUOp, e_BSel, e_ASel, e_ctrl[0]}));  // open: clr
  Register #(.width(32)) register_2 (.D(d_pc), .en(nmstall), .clk(clk), .Q(e_pc));  // open: clr
  Register #(.width(32)) register_3 (.D(d_r1), .en(nmstall), .clk(clk), .Q(e_r1));  // open: clr
  Register #(.width(32)) register_4 (.D(d_r2), .en(nmstall), .clk(clk), .Q(e_r2));  // open: clr
  Register #(.width(32)) register_5 (.D(d_imm), .en(nmstall), .clk(clk), .Q(e_imm));  // open: clr
  Register #(.width(6)) register_6 (.D(d_rs1), .en(nmstall), .clk(clk), .Q(e_rs1));  // open: clr
  Register #(.width(6)) register_7 (.D(d_rs2), .en(nmstall), .clk(clk), .Q(e_rs2));  // open: clr
  Register #(.width(6)) register_8 (.D(d_rd), .en(nmstall), .clk(clk), .Q(e_rd));  // open: clr
  Register #(.width(3)) register_9 (.D(d_f3), .en(nmstall), .clk(clk), .Q(e_f3));  // open: clr
  Register #(.width(1)) register_10 (.D(d_pt_q), .en(nmstall), .clk(clk), .Q(e_pt));  // open: clr
  Register #(.width(32)) register_11 (.D(d_ptgt), .en(nmstall), .clk(clk), .Q(e_ptgt));  // open: clr

  assign {e_ctrl[23], e_ctrl[16], e_ctrl[7:1]} = {e_Csr, e_Branch, e_ALUOp, e_BSel, e_ASel};
  assign e_FpOp = e_ctrl[28:25];
  assign e_Jal = e_ctrl[17];
  assign e_Jalr = e_ctrl[18];
  assign e_MemRead = e_ctrl[8];
  assign e_Mret = e_ctrl[24];
  assign e_ResSel = e_ctrl[12:10];
  assign e_Valid = e_ctrl[22];
endmodule

module CSRUnit (
  input  [31:0] e_imm,
  input  [5:0] e_rs1,
  output [11:0] e_csra,
  output [4:0] e_zimm
);


  assign e_csra = e_imm[11:0];
  assign e_zimm = e_rs1[4:0];
endmodule

module RedirectUnit (
  input  e_Branch,
  input  e_Csr,
  input  e_Jal,
  input  e_Jalr,
  input  e_Mret,
  input  e_Valid,
  input  [31:0] e_brt,
  input  e_cond,
  input  [31:0] e_ctrl,
  input  [31:0] e_jalrt,
  input  [31:0] e_pc4,
  input  e_pt,
  input  [31:0] e_ptgt,
  input  irq,
  input  [31:0] mepc,
  input  [31:0] mtvec,
  input  nmstall,
  output br_ev,
  output btb_we,
  output csr_we,
  output e_actual,
  output [31:0] e_ctrl_q,
  output [31:0] e_target,
  output mis_ev,
  output redir,
  output [31:0] redir_tgt,
  output take
);

  wire and_1_out, and_7_out, comparator_1_eq, dirmis, e_isbr, e_isbr2, e_mret_x, ntake, or_4_out, tgtne;
  wire [31:0] bp_tgt, multiplexer_4_out;

  and and_1 (and_1_out, e_Branch, e_cond);
  Multiplexer #(.width(32), .select(1)) multiplexer_1 (.in0(e_brt), .in1(e_jalrt), .out(e_target), .sel(e_Jalr));
  and and_2 (take, irq, e_Valid, nmstall);
  or or_1 (e_isbr, e_Branch, e_Jal, e_Jalr);
  or or_2 (e_isbr2, e_Branch, e_Jal, e_Jalr);
  not not_1 (ntake, take);
  Comparator #(.width(32), .mode("unsigned")) comparator_1 (
    .a(e_target), .b(e_ptgt), .eq(comparator_1_eq));  // open: gt, lt
  Multiplexer #(.width(32), .select(1)) multiplexer_2 (.in0(e_ctrl), .in1({32{1'b0}}), .out(e_ctrl_q), .sel(take));
  or or_3 (e_actual, and_1_out, e_Jal, e_Jalr);
  xor xor_1 (dirmis, e_actual, e_pt);
  not not_2 (tgtne, comparator_1_eq);
  Multiplexer #(.width(32), .select(1)) multiplexer_3 (.in0(e_pc4), .in1(e_target), .out(bp_tgt), .sel(e_actual));
  and and_3 (btb_we, e_isbr, ntake, nmstall);
  and and_4 (e_mret_x, e_Mret, ntake);
  and and_5 (csr_we, e_Csr, ntake);
  and and_6 (br_ev, e_isbr2, ntake, nmstall);
  and and_7 (and_7_out, e_actual, tgtne);
  Multiplexer #(.width(32), .select(1)) multiplexer_4 (.in0(bp_tgt), .in1(mepc), .out(multiplexer_4_out), .sel(e_Mret));
  or or_4 (or_4_out, dirmis, and_7_out);
  Multiplexer #(.width(32), .select(1)) multiplexer_5 (
    .in0(multiplexer_4_out), .in1(mtvec), .out(redir_tgt), .sel(take));
  or or_5 (redir, take, e_mret_x, or_4_out);
  and and_8 (mis_ev, or_4_out, ntake, nmstall);
endmodule

module EX_MEM (
  input  clk,
  input  [31:0] e_ctrl_q,
  input  [2:0] e_f3,
  input  [5:0] e_rd,
  input  [31:0] e_res,
  input  [5:0] e_rs2,
  input  [31:0] fb,
  input  nmstall,
  output m_MemRead,
  output m_MemWrite,
  output m_RegWrite,
  output [31:0] m_ctrl,
  output [2:0] m_f3,
  output [31:0] m_r2,
  output [5:0] m_rd,
  output [31:0] m_res,
  output [5:0] m_rs2
);

  Register #(.width(32)) register_1 (.D(e_ctrl_q), .en(nmstall), .clk(clk), .Q(m_ctrl));  // open: clr
  Register #(.width(32)) register_2 (.D(e_res), .en(nmstall), .clk(clk), .Q(m_res));  // open: clr
  Register #(.width(32)) register_3 (.D(fb), .en(nmstall), .clk(clk), .Q(m_r2));  // open: clr
  Register #(.width(6)) register_4 (.D(e_rd), .en(nmstall), .clk(clk), .Q(m_rd));  // open: clr
  Register #(.width(3)) register_5 (.D(e_f3), .en(nmstall), .clk(clk), .Q(m_f3));  // open: clr
  Register #(.width(6)) register_6 (.D(e_rs2), .en(nmstall), .clk(clk), .Q(m_rs2));  // open: clr

  assign m_MemRead = m_ctrl[8];
  assign m_MemWrite = m_ctrl[9];
  assign m_RegWrite = m_ctrl[0];
endmodule

module MemFwd (
  input  m_MemWrite,
  input  [31:0] m_r2,
  input  [5:0] m_rs2,
  input  w_RegWrite,
  input  [31:0] w_data,
  input  [5:0] w_rd,
  input  w_rdnz,
  output [31:0] m_r2f
);

  wire comparator_1_eq, sfw;

  Comparator #(.width(6), .mode("unsigned")) comparator_1 (.a(w_rd), .b(m_rs2), .eq(comparator_1_eq));  // open: gt, lt
  and and_1 (sfw, m_MemWrite, w_RegWrite, w_rdnz, comparator_1_eq);
  Multiplexer #(.width(32), .select(1)) multiplexer_1 (.in0(m_r2), .in1(w_data), .out(m_r2f), .sel(sfw));
endmodule

module CacheCtrl (
  input  [31:0] c_data,
  input  c_hit,
  input  clk,
  input  [31:0] io_data,
  input  isio,
  input  m_MemRead,
  input  m_MemWrite,
  input  [31:0] m_mraw,
  output c_fill,
  output c_wr,
  output dc_hit_ev,
  output dmem_we,
  output io_we,
  output [31:0] m_src,
  output mstall,
  output nmstall
);

  wire c_miss, c_nhit, c_rd, mc_done, mc_nd, not_1_out, not_4_out;
  wire [1:0] mcnt, mcnt1, multiplexer_3_out;
  wire [31:0] multiplexer_1_out;

  not not_1 (not_1_out, isio);
  not not_2 (c_nhit, c_hit);
  Multiplexer #(.width(32), .select(1)) multiplexer_1 (
    .in0(m_mraw), .in1(c_data), .out(multiplexer_1_out), .sel(c_hit));
  not not_3 (mc_nd, mc_done);
  Adder #(.width(2)) adder_1 (.a(mcnt), .b(2'b01), .out(mcnt1));  // open: cin, cout
  Multiplexer #(.width(32), .select(1)) multiplexer_2 (.in0(multiplexer_1_out), .in1(io_data), .out(m_src), .sel(isio));
  and and_1 (dmem_we, m_MemWrite, not_1_out);
  and and_2 (c_rd, m_MemRead, not_1_out);
  and and_3 (c_wr, m_MemWrite, not_1_out);
  and and_4 (c_miss, c_rd, c_nhit);
  and and_5 (mstall, c_miss, mc_nd);
  not not_4 (not_4_out, c_miss);
  not not_5 (nmstall, mstall);
  Multiplexer #(.width(2), .select(1)) multiplexer_3 (.in0(2'b00), .in1(mcnt1), .out(multiplexer_3_out), .sel(mstall));
  and and_6 (dc_hit_ev, c_rd, not_4_out);
  Register #(.width(2)) register_1 (.D(multiplexer_3_out), .clk(clk), .Q(mcnt));  // open: en, clr
  and and_7 (io_we, m_MemWrite, nmstall);
  Comparator #(.width(2), .mode("unsigned")) comparator_1 (.a(mcnt), .b(2'b11), .eq(mc_done));  // open: gt, lt
  and and_8 (c_fill, c_miss, mc_done);
endmodule

module MEM_WB (
  input  clk,
  input  [31:0] m_ctrl,
  input  [31:0] m_mdata,
  input  [5:0] m_rd,
  input  [31:0] m_res,
  input  nmstall,
  output w_Halt,
  output w_MemRead,
  output w_RegWrite,
  output w_Valid,
  output [31:0] w_mdata,
  output [5:0] w_rd,
  output [31:0] w_res
);

  wire [31:1] register_1_q;

  Register #(.width(32)) register_1 (
    .D(m_ctrl), .en(nmstall), .clk(clk),
    .Q({register_1_q[31:23], w_Valid, register_1_q[21:20], w_Halt, register_1_q[18:9], w_MemRead, register_1_q[7:1], w_RegWrite}));  // open: clr
  Register #(.width(32)) register_2 (.D(m_res), .en(nmstall), .clk(clk), .Q(w_res));  // open: clr
  Register #(.width(32)) register_3 (.D(m_mdata), .en(nmstall), .clk(clk), .Q(w_mdata));  // open: clr
  Register #(.width(6)) register_4 (.D(m_rd), .en(nmstall), .clk(clk), .Q(w_rd));  // open: clr
endmodule

module PerfCounters (
  input  br_ev,
  input  c_fill,
  input  clk,
  input  dc_hit_ev,
  input  mis_ev,
  input  nmstall,
  input  w_Valid,
  output [31:0] br_cnt,
  output [31:0] br_miss,
  output [31:0] cycles,
  output [31:0] dc_hit,
  output [31:0] dc_miss,
  output [31:0] instret
);

  wire ret_ev;
  wire [31:0] adder_1_out, adder_2_out, adder_3_out, adder_4_out, adder_5_out, adder_6_out,
       multiplexer_1_out, multiplexer_2_out, multiplexer_3_out, multiplexer_4_out, multiplexer_5_out;

  and and_1 (ret_ev, w_Valid, nmstall);
  Adder #(.width(32)) adder_1 (.a(cycles), .b(32'h1), .out(adder_1_out));  // open: cin, cout
  Multiplexer #(.width(32), .select(1)) multiplexer_1 (
    .in0({32{1'b0}}), .in1(32'h1), .out(multiplexer_1_out), .sel(br_ev));
  Multiplexer #(.width(32), .select(1)) multiplexer_2 (
    .in0({32{1'b0}}), .in1(32'h1), .out(multiplexer_2_out), .sel(mis_ev));
  Multiplexer #(.width(32), .select(1)) multiplexer_3 (
    .in0({32{1'b0}}), .in1(32'h1), .out(multiplexer_3_out), .sel(dc_hit_ev));
  Multiplexer #(.width(32), .select(1)) multiplexer_4 (
    .in0({32{1'b0}}), .in1(32'h1), .out(multiplexer_4_out), .sel(c_fill));
  Register #(.width(32)) register_1 (.D(adder_1_out), .clk(clk), .Q(cycles));  // open: en, clr
  Multiplexer #(.width(32), .select(1)) multiplexer_5 (
    .in0({32{1'b0}}), .in1(32'h1), .out(multiplexer_5_out), .sel(ret_ev));
  Adder #(.width(32)) adder_2 (.a(br_cnt), .b(multiplexer_1_out), .out(adder_2_out));  // open: cin, cout
  Adder #(.width(32)) adder_3 (.a(br_miss), .b(multiplexer_2_out), .out(adder_3_out));  // open: cin, cout
  Adder #(.width(32)) adder_4 (.a(dc_hit), .b(multiplexer_3_out), .out(adder_4_out));  // open: cin, cout
  Adder #(.width(32)) adder_5 (.a(dc_miss), .b(multiplexer_4_out), .out(adder_5_out));  // open: cin, cout
  Register #(.width(32)) register_2 (.D(adder_2_out), .clk(clk), .Q(br_cnt));  // open: en, clr
  Register #(.width(32)) register_3 (.D(adder_3_out), .clk(clk), .Q(br_miss));  // open: en, clr
  Register #(.width(32)) register_4 (.D(adder_4_out), .clk(clk), .Q(dc_hit));  // open: en, clr
  Register #(.width(32)) register_5 (.D(adder_5_out), .clk(clk), .Q(dc_miss));  // open: en, clr
  Adder #(.width(32)) adder_6 (.a(instret), .b(multiplexer_5_out), .out(adder_6_out));  // open: cin, cout
  Register #(.width(32)) register_6 (.D(adder_6_out), .clk(clk), .Q(instret));  // open: en, clr
endmodule
