// Logisim project RiscV_SingleCycle_hdl_v3.circ as structural Verilog: 12 circuits, main circuit main
module main (
  output halt,
  output [31:0] PC_out,
  output [31:0] cycles
);

  wire and_1_out, Branch, branchunit_1_cond, BSel, clk, Jal, Jalr, maincontrol_1_regwrite, MemRead, MemWrite,
       taken;
  wire [1:0] ASel, boff;
  wire [2:0] f3, maincontrol_1_immsel, ResSel;
  wire [3:0] ALUOp;
  wire [4:0] rd, rs1, rs2;
  wire [9:0] daddr;
  wire [31:0] brt, immgen_1_imm, instr, jalrt, loadunit_1_v, mraw, muldiv_1_y, multiplexer_1_out,
       multiplexer_2_out, multiplexer_3_out, multiplexer_4_out, pc4, r1, r2, res, storeunit_1_new, wb;
  wire [31:12] alu_1_y;

  Multiplexer #(.width(32), .select(1)) multiplexer_1 (.in0(pc4), .in1(brt), .out(multiplexer_1_out), .sel(taken));
  Clock clock_1 (.out(clk));
  PerfCounters perfcounters_1 (.clk(clk), .cycles(cycles));
  Multiplexer #(.width(32), .select(1)) multiplexer_2 (
    .in0(multiplexer_1_out), .in1(jalrt), .out(multiplexer_2_out), .sel(Jalr));
  Register #(.width(32)) register_1 (.D(multiplexer_2_out), .clk(clk), .Q(PC_out));  // open: en, clr
  Adder #(.width(32)) adder_1 (.a(PC_out), .b(32'h4), .out(pc4));  // open: cin, cout
  ROM #(.addrWidth(10), .dataWidth(32)) IMEM (.addr(PC_out[11:2]), .data(instr));
  InstrDecode instrdecode_1 (.instr(instr), .f3(f3), .rd(rd), .rs1(rs1), .rs2(rs2));
  MainControl maincontrol_1 (
    .instr(instr), .ALUOp(ALUOp), .ASel(ASel), .BSel(BSel), .Branch(Branch), .Halt(halt),
    .ImmSel(maincontrol_1_immsel), .Jal(Jal), .Jalr(Jalr), .MemRead(MemRead), .MemWrite(MemWrite),
    .RegWrite(maincontrol_1_regwrite), .ResSel(ResSel));
  RegFile regfile_1 (.clk(clk), .we(maincontrol_1_regwrite), .rs1(rs1), .rs2(rs2), .rd(rd), .wd(wb), .r1(r1), .r2(r2));
  ImmGen immgen_1 (.instr(instr), .sel(maincontrol_1_immsel), .imm(immgen_1_imm));
  BranchUnit branchunit_1 (.a(r1), .b(r2), .f3(f3), .cond(branchunit_1_cond));
  Multiplexer #(.width(32), .select(2)) multiplexer_3 (
    .in0(r1), .in1(PC_out), .in2({32{1'b0}}), .out(multiplexer_3_out), .sel(ASel));  // open: in3
  Multiplexer #(.width(32), .select(1)) multiplexer_4 (
    .in0(r2), .in1(immgen_1_imm), .out(multiplexer_4_out), .sel(BSel));
  Adder #(.width(32)) adder_2 (.a(PC_out), .b(immgen_1_imm), .out(brt));  // open: cin, cout
  ALU alu_1 (.a(multiplexer_3_out), .b(multiplexer_4_out), .op(ALUOp), .y({alu_1_y, daddr, boff}));
  MulDiv muldiv_1 (.a(r1), .b(r2), .f3(f3), .y(muldiv_1_y));
  and and_1 (and_1_out, Branch, branchunit_1_cond);
  assign jalrt = {alu_1_y, daddr, boff} & 32'hfffffffe;  // AND_Gate and_2, 32 bits wide
  or or_1 (taken, and_1_out, Jal);
  Multiplexer #(.width(32), .select(3)) multiplexer_5 (
    .in0({alu_1_y, daddr, boff}), .in1(pc4), .in2(muldiv_1_y), .in3({32{1'b0}}), .in4({32{1'b0}}),
    .in5({32{1'b0}}), .in6({32{1'b0}}), .in7({32{1'b0}}), .out(res), .sel(ResSel));
  StoreUnit storeunit_1 (.old(mraw), .wd(r2), .off(boff), .f3(f3), .\new (storeunit_1_new));
  RAM #(.addrWidth(10), .dataWidth(32), .asyncread("true")) DMEM (
    .addr(daddr), .we(MemWrite), .oe(1'b1), .clk(clk), .din(storeunit_1_new), .dout(mraw));
  LoadUnit loadunit_1 (.din(mraw), .off(boff), .f3(f3), .v(loadunit_1_v));
  Multiplexer #(.width(32), .select(1)) multiplexer_6 (.in0(res), .in1(loadunit_1_v), .out(wb), .sel(MemRead));

  // Other names for the same wires on the sheet: pc[31:0] = PC_out

  // Notes on the sheet:
  //   PC next
  //   PC
  //   contents of IMEM (hex, n*v repeats v):
  //   93 100113 193 c00213 11a023 2082b3 10093 28113 418193 fff20213 fe0214e3 313 193 c00213 1a383 730333
  //   418193 fff20213 fe0218e3 73
  //   IMEM
  //   Decode / Control
  //   RegFile / Imm
  //   ALU / MulDiv
  //   DMEM
  //   Write-back
endmodule

module ALU (
  input  [31:0] a,
  input  [31:0] b,
  input  [3:0] op,
  output [31:0] y
);

  wire comparator_1_lt, comparator_2_lt;
  wire [31:0] add, \and , bit_extender_1_out, bit_extender_2_out, \or , shifter_1_out, shifter_2_out,
       shifter_3_out, sub, \xor ;

  Adder #(.width(32)) adder_1 (.a(a), .b(b), .out(add));  // open: cin, cout
  Subtractor #(.width(32)) subtractor_1 (.a(a), .b(b), .out(sub));  // open: bin, bout
  Comparator #(.width(32), .mode("twosComplement")) comparator_1 (.a(a), .b(b), .lt(comparator_1_lt));  // open: gt, eq
  Comparator #(.width(32), .mode("unsigned")) comparator_2 (.a(a), .b(b), .lt(comparator_2_lt));  // open: gt, eq
  assign \xor  = a ^ b;  // XOR_Gate xor_1, 32 bits wide
  assign \or  = a | b;  // OR_Gate or_1, 32 bits wide
  assign \and  = a & b;  // AND_Gate and_1, 32 bits wide
  Shifter #(.width(32), .shift("ll")) shifter_1 (.in(a), .\dist (b[4:0]), .out(shifter_1_out));
  Shifter #(.width(32), .shift("lr")) shifter_2 (.in(a), .\dist (b[4:0]), .out(shifter_2_out));
  Shifter #(.width(32), .shift("ar")) shifter_3 (.in(a), .\dist (b[4:0]), .out(shifter_3_out));
  assign bit_extender_1_out = {{31{1'b0}}, comparator_1_lt};  // Bit_Extender bit_extender_1
  assign bit_extender_2_out = {{31{1'b0}}, comparator_2_lt};  // Bit_Extender bit_extender_2
  Multiplexer #(.width(32), .select(4)) multiplexer_1 (
    .in0(add), .in1(sub), .in2(shifter_1_out), .in3(bit_extender_1_out), .in4(bit_extender_2_out),
    .in5(\xor ), .in6(shifter_2_out), .in7(shifter_3_out), .in8(\or ), .in9(\and ), .in10({32{1'b0}}),
    .in11({32{1'b0}}), .in12({32{1'b0}}), .in13({32{1'b0}}), .in14({32{1'b0}}), .in15({32{1'b0}}), .out(y),
    .sel(op));
endmodule

module RegFile (
  input  clk,
  input  we,
  input  [4:0] rs1,
  input  [4:0] rs2,
  input  [4:0] rd,
  input  [31:0] wd,
  output [31:0] r1,
  output [31:0] r2
);

  wire and_1_out, and_2_out, and_3_out, and_4_out, and_5_out, and_6_out, and_7_out, and_8_out, and_9_out,
       and_10_out, and_11_out, and_12_out, and_13_out, and_14_out, and_15_out, and_16_out, and_17_out,
       and_18_out, and_19_out, and_20_out, and_21_out, and_22_out, and_23_out, and_24_out, and_25_out,
       and_26_out, and_27_out, and_28_out, and_29_out, and_30_out, and_31_out, dec1, dec2, dec3, dec4, dec12,
       dec20, dec28, decoder_1_out5, decoder_1_out6, decoder_1_out7, decoder_1_out8, decoder_1_out9,
       decoder_1_out10, decoder_1_out11, decoder_1_out13, decoder_1_out14, decoder_1_out15, decoder_1_out16,
       decoder_1_out17, decoder_1_out18, decoder_1_out19, decoder_1_out21, decoder_1_out22, decoder_1_out23,
       decoder_1_out24, decoder_1_out25, decoder_1_out26, decoder_1_out27, decoder_1_out29, decoder_1_out30,
       decoder_1_out31;
  wire [31:0] register_4_q, register_7_q, register_8_q, register_9_q, register_11_q, register_12_q,
       register_13_q, register_15_q, register_16_q, register_17_q, register_18_q, register_19_q,
       register_20_q, register_21_q, register_23_q, register_24_q, register_25_q, register_27_q,
       register_28_q, register_29_q, register_30_q, register_31_q, x1, x2, x3, x5, x6, x10, x14, x22, x26;

  Decoder #(.select(5), .enable("false")) decoder_1 (
    .out1(dec1), .out2(dec2), .out3(dec3), .out4(dec4), .out5(decoder_1_out5), .out6(decoder_1_out6),
    .out7(decoder_1_out7), .out8(decoder_1_out8), .out9(decoder_1_out9), .out10(decoder_1_out10),
    .out11(decoder_1_out11), .out12(dec12), .out13(decoder_1_out13), .out14(decoder_1_out14),
    .out15(decoder_1_out15), .out16(decoder_1_out16), .out17(decoder_1_out17), .out18(decoder_1_out18),
    .out19(decoder_1_out19), .out20(dec20), .out21(decoder_1_out21), .out22(decoder_1_out22),
    .out23(decoder_1_out23), .out24(decoder_1_out24), .out25(decoder_1_out25), .out26(decoder_1_out26),
    .out27(decoder_1_out27), .out28(dec28), .out29(decoder_1_out29), .out30(decoder_1_out30),
    .out31(decoder_1_out31), .sel(rd));  // open: out0
  and and_1 (and_1_out, we, dec1);
  and and_2 (and_2_out, we, dec2);
  and and_3 (and_3_out, we, dec3);
  and and_4 (and_4_out, we, dec4);
  and and_5 (and_5_out, we, decoder_1_out5);
  and and_6 (and_6_out, we, decoder_1_out6);
  and and_7 (and_7_out, we, decoder_1_out7);
  and and_8 (and_8_out, we, decoder_1_out8);
  and and_9 (and_9_out, we, decoder_1_out9);
  and and_10 (and_10_out, we, decoder_1_out10);
  and and_11 (and_11_out, we, decoder_1_out11);
  and and_12 (and_12_out, we, dec12);
  and and_13 (and_13_out, we, decoder_1_out13);
  and and_14 (and_14_out, we, decoder_1_out14);
  and and_15 (and_15_out, we, decoder_1_out15);
  and and_16 (and_16_out, we, decoder_1_out16);
  and and_17 (and_17_out, we, decoder_1_out17);
  and and_18 (and_18_out, we, decoder_1_out18);
  and and_19 (and_19_out, we, decoder_1_out19);
  and and_20 (and_20_out, we, dec20);
  and and_21 (and_21_out, we, decoder_1_out21);
  and and_22 (and_22_out, we, decoder_1_out22);
  and and_23 (and_23_out, we, decoder_1_out23);
  and and_24 (and_24_out, we, decoder_1_out24);
  and and_25 (and_25_out, we, decoder_1_out25);
  and and_26 (and_26_out, we, decoder_1_out26);
  and and_27 (and_27_out, we, decoder_1_out27);
  and and_28 (and_28_out, we, dec28);
  and and_29 (and_29_out, we, decoder_1_out29);
  and and_30 (and_30_out, we, decoder_1_out30);
  and and_31 (and_31_out, we, decoder_1_out31);
  Register #(.width(32)) register_1 (.D(wd), .en(and_1_out), .clk(clk), .Q(x1));  // open: clr
  Register #(.width(32)) register_2 (.D(wd), .en(and_2_out), .clk(clk), .Q(x2));  // open: clr
  Register #(.width(32)) register_3 (.D(wd), .en(and_3_out), .clk(clk), .Q(x3));  // open: clr
  Register #(.width(32)) register_4 (.D(wd), .en(and_4_out), .clk(clk), .Q(register_4_q));  // open: clr
  Register #(.width(32)) register_5 (.D(wd), .en(and_5_out), .clk(clk), .Q(x5));  // open: clr
  Register #(.width(32)) register_6 (.D(wd), .en(and_6_out), .clk(clk), .Q(x6));  // open: clr
  Register #(.width(32)) register_7 (.D(wd), .en(and_7_out), .clk(clk), .Q(register_7_q));  // open: clr
  Register #(.width(32)) register_8 (.D(wd), .en(and_8_out), .clk(clk), .Q(register_8_q));  // open: clr
  Register #(.width(32)) register_9 (.D(wd), .en(and_9_out), .clk(clk), .Q(register_9_q));  // open: clr
  Register #(.width(32)) register_10 (.D(wd), .en(and_10_out), .clk(clk), .Q(x10));  // open: clr
  Register #(.width(32)) register_11 (.D(wd), .en(and_11_out), .clk(clk), .Q(register_11_q));  // open: clr
  Register #(.width(32)) register_12 (.D(wd), .en(and_12_out), .clk(clk), .Q(register_12_q));  // open: clr
  Register #(.width(32)) register_13 (.D(wd), .en(and_13_out), .clk(clk), .Q(register_13_q));  // open: clr
  Register #(.width(32)) register_14 (.D(wd), .en(and_14_out), .clk(clk), .Q(x14));  // open: clr
  Register #(.width(32)) register_15 (.D(wd), .en(and_15_out), .clk(clk), .Q(register_15_q));  // open: clr
  Register #(.width(32)) register_16 (.D(wd), .en(and_16_out), .clk(clk), .Q(register_16_q));  // open: clr
  Register #(.width(32)) register_17 (.D(wd), .en(and_17_out), .clk(clk), .Q(register_17_q));  // open: clr
  Register #(.width(32)) register_18 (.D(wd), .en(and_18_out), .clk(clk), .Q(register_18_q));  // open: clr
  Register #(.width(32)) register_19 (.D(wd), .en(and_19_out), .clk(clk), .Q(register_19_q));  // open: clr
  Register #(.width(32)) register_20 (.D(wd), .en(and_20_out), .clk(clk), .Q(register_20_q));  // open: clr
  Register #(.width(32)) register_21 (.D(wd), .en(and_21_out), .clk(clk), .Q(register_21_q));  // open: clr
  Register #(.width(32)) register_22 (.D(wd), .en(and_22_out), .clk(clk), .Q(x22));  // open: clr
  Register #(.width(32)) register_23 (.D(wd), .en(and_23_out), .clk(clk), .Q(register_23_q));  // open: clr
  Register #(.width(32)) register_24 (.D(wd), .en(and_24_out), .clk(clk), .Q(register_24_q));  // open: clr
  Register #(.width(32)) register_25 (.D(wd), .en(and_25_out), .clk(clk), .Q(register_25_q));  // open: clr
  Register #(.width(32)) register_26 (.D(wd), .en(and_26_out), .clk(clk), .Q(x26));  // open: clr
  Register #(.width(32)) register_27 (.D(wd), .en(and_27_out), .clk(clk), .Q(register_27_q));  // open: clr
  Register #(.width(32)) register_28 (.D(wd), .en(and_28_out), .clk(clk), .Q(register_28_q));  // open: clr
  Register #(.width(32)) register_29 (.D(wd), .en(and_29_out), .clk(clk), .Q(register_29_q));  // open: clr
  Register #(.width(32)) register_30 (.D(wd), .en(and_30_out), .clk(clk), .Q(register_30_q));  // open: clr
  Register #(.width(32)) register_31 (.D(wd), .en(and_31_out), .clk(clk), .Q(register_31_q));  // open: clr
  Multiplexer #(.width(32), .select(5)) multiplexer_1 (
    .in0({32{1'b0}}), .in1(x1), .in2(x2), .in3(x3), .in4(register_4_q), .in5(x5), .in6(x6),
    .in7(register_7_q), .in8(register_8_q), .in9(register_9_q), .in10(x10), .in11(register_11_q),
    .in12(register_12_q), .in13(register_13_q), .in14(x14), .in15(register_15_q), .in16(register_16_q),
    .in17(register_17_q), .in18(register_18_q), .in19(register_19_q), .in20(register_20_q),
    .in21(register_21_q), .in22(x22), .in23(register_23_q), .in24(register_24_q), .in25(register_25_q),
    .in26(x26), .in27(register_27_q), .in28(register_28_q), .in29(register_29_q), .in30(register_30_q),
    .in31(register_31_q), .out(r1), .sel(rs1));
  Multiplexer #(.width(32), .select(5)) multiplexer_2 (
    .in0({32{1'b0}}), .in1(x1), .in2(x2), .in3(x3), .in4(register_4_q), .in5(x5), .in6(x6),
    .in7(register_7_q), .in8(register_8_q), .in9(register_9_q), .in10(x10), .in11(register_11_q),
    .in12(register_12_q), .in13(register_13_q), .in14(x14), .in15(register_15_q), .in16(register_16_q),
    .in17(register_17_q), .in18(register_18_q), .in19(register_19_q), .in20(register_20_q),
    .in21(register_21_q), .in22(x22), .in23(register_23_q), .in24(register_24_q), .in25(register_25_q),
    .in26(x26), .in27(register_27_q), .in28(register_28_q), .in29(register_29_q), .in30(register_30_q),
    .in31(register_31_q), .out(r2), .sel(rs2));
endmodule

module ImmGen (
  input  [31:0] instr,
  input  [2:0] sel,
  output [31:0] imm
);

  wire [31:0] bit_extender_2_out, bit_extender_3_out, bit_extender_4_out, immI;

  assign immI = {{20{instr[31]}}, instr[31:20]};  // Bit_Extender bit_extender_1
  assign bit_extender_2_out = {{20{instr[31]}}, {instr[31:25], instr[11:7]}};  // Bit_Extender bit_extender_2
  assign bit_extender_3_out = {{19{instr[31]}}, {instr[31], instr[7], instr[30:25], instr[11:8], 1'b0}};  // Bit_Extender bit_extender_3
  assign bit_extender_4_out = {{11{instr[31]}}, {instr[31], instr[19:12], instr[20], instr[30:21], 1'b0}};  // Bit_Extender bit_extender_4
  Multiplexer #(.width(32), .select(3)) multiplexer_1 (
    .in0(immI), .in1(bit_extender_2_out), .in2(bit_extender_3_out), .in3({instr[31:12], {12{1'b0}}}),
    .in4(bit_extender_4_out), .in5({32{1'b0}}), .in6({32{1'b0}}), .in7({32{1'b0}}), .out(imm), .sel(sel));

  // Other names for the same wires on the sheet: b4_1[3:0] = instr[11:8];
  //   b13[12:1] = {instr[31], instr[7], instr[30:25], instr[11:8]}; s12[11:0] = {instr[31:25], instr[11:7]};
  //   s_lo[4:0] = instr[11:7]; b11 = instr[7]; immU[31:12] = instr[31:12]; j10_1[9:0] = instr[30:21];
  //   j21[20:1] = {instr[31], instr[19:12], instr[20], instr[30:21]}; u20[19:0] = instr[31:12];
  //   b10_5[5:0] = instr[30:25]; s_hi[6:0] = instr[31:25]; j11 = instr[20]; j19_12[7:0] = instr[19:12];
  //   b12 = instr[31]
endmodule

module BranchUnit (
  input  [31:0] a,
  input  [31:0] b,
  input  [2:0] f3,
  output cond
);

  wire eq, lts, ltu, not_1_out, not_2_out, not_3_out;

  Comparator #(.width(32), .mode("twosComplement")) comparator_1 (.a(a), .b(b), .eq(eq), .lt(lts));  // open: gt
  Comparator #(.width(32), .mode("unsigned")) comparator_2 (.a(a), .b(b), .lt(ltu));  // open: gt, eq
  not not_1 (not_1_out, eq);
  not not_2 (not_2_out, lts);
  not not_3 (not_3_out, ltu);
  Multiplexer #(.width(1), .select(3)) multiplexer_1 (
    .in0(eq), .in1(not_1_out), .in2(1'b0), .in3(1'b0), .in4(lts), .in5(not_2_out), .in6(ltu),
    .in7(not_3_out), .out(cond), .sel(f3));
endmodule

module Control (
  input  [31:0] instr,
  output [31:0] ctrl
);

  wire qok;
  wire [31:0] CTRL_data;

  and and_1 (qok, instr[0], instr[1]);
  ROM #(.addrWidth(16), .dataWidth(32)) u_CTRL (
    .addr({instr[20], instr[31:25], instr[14:12], instr[6:2]}), .data(CTRL_data));
  Multiplexer #(.width(32), .select(1)) multiplexer_1 (.in0({32{1'b0}}), .in1(CTRL_data), .out(ctrl), .sel(qok));

  // Other names for the same wires on the sheet: caddr[15:0] = {instr[20], instr[31:25], instr[14:12], instr[6:2]};
  //   op5[4:0] = instr[6:2]; f3[2:0] = instr[14:12]; f7[6:0] = instr[31:25]; b20 = instr[20]

  // Notes on the sheet:
  //   contents of CTRL (hex, n*v repeats v):
  //   500109 3*0 500009 40600b 2*0 702208 3*0 700001 40600d 6*0 e0701001 3*0 714000 540409 0 428401 480000
  //   3*0 500109 3*0 500029 40600b 2*0 702208 3*0 700021 40600d 6*0 e0701001 3*0 714000 2*0 428401 d00c01
  //   3*0 500109 20500109 2*0 500039 40600b 2*0 702208 80702208 2*0 700031 40600d 6*0 e0701001 6*0 428401
  //   d00c01 7*0 500049 40600b 6*0 700041 40600d 6*0 e0701001 6*0 428401 d00c01 3*0 500109 3*0 500059
  //   40600b 6*0 700051 40600d 6*0 e0701001 3*0 714000 2*0 428401 4*0 500109 3*0 500069 40600b 6*0 700061
  //   40600d 6*0 e0701001 3*0 714000 2*0 428401 c00c01 7*0 500089 40600b 6*0 700081 40600d 6*0 e0701001
  //   3*0 714000 2*0 428401 c00c01 7*0 500099 40600b 6*0 700091 40600d 6*0 e0701001 3*0 714000 2*0 428401
  //   c00c01 3*0 500109 3*0 500009 40600b 2*0 702208 3*0 700801 40600d 10*0 714000 540409 0 428401 480000
  //   3*0 500109 4*0 40600b 2*0 702208 3*0 700801 40600d 10*0 714000 2*0 428401 d00c01 3*0 500109 20500109
  //   2*0 500039 40600b 2*0 702208 80702208 2*0 700801 40600d 13*0 428401 d00c01 7*0 500049 40600b 6*0
  //   700801 40600d 13*0 428401 d00c01 3*0 500109 3*0 500059 40600b 6*0 700801 40600d 10*0 714000 2*0
  //   428401 4*0 500109 4*0 40600b 6*0 700801 40600d 10*0 714000 2*0 428401 c00c01 7*0 500089 40600b 6*0
  //   700801 40600d 10*0 714000 2*0 428401 c00c01 7*0 500099 40600b 6*0 700801 40600d 10*0 714000 2*0
  //   428401 c00c01 3*0 500109 3*0 500009 40600b 2*0 702208 4*0 40600d 10*0 714000 540409 0 428401 480000
  //   3*0 500109 4*0 40600b 2*0 702208 4*0 40600d 10*0 714000 2*0 428401 d00c01 3*0 500109 20500109 2*0
  //   500039 40600b 2*0 702208 80702208 3*0 40600d 13*0 428401 d00c01 7*0 500049 40600b 7*0 40600d 13*0
  //   428401 d00c01 3*0 500109 3*0 500059 40600b 7*0 40600d 10*0 714000 2*0 428401 4*0 500109 4*0 40600b
  //   7*0 40600d 10*0 714000 2*0 428401 c00c01 7*0 500089 40600b 7*0 40600d 10*0 714000 2*0 428401 c00c01
  //   7*0 500099 40600b 7*0 40600d 10*0 714000 2*0 428401 c00c01 3*0 500109 3*0 500009 40600b 2*0 702208
  //   4*0 40600d 10*0 714000 540409 0 428401 480000 3*0 500109 4*0 40600b 2*0 702208 4*0 40600d 10*0
  //   714000 2*0 428401 d00c01 3*0 500109 20500109 2*0 500039 40600b 2*0 702208 80702208 3*0 40600d 13*0
  //   428401 d00c01 7*0 500049 40600b 7*0 40600d 13*0 428401 d00c01 3*0 500109 3*0 500059 40600b 7*0
  //   40600d 10*0 714000 2*0 428401 4*0 500109 4*0 40600b 7*0 40600d 10*0 714000 2*0 428401 c00c01 7*0
  //   500089 40600b 7*0 40600d 10*0 714000 2*0 428401 c00c01 7*0 500099 40600b 7*0 40600d 10*0 714000 2*0
  //   428401 c00c01 3*0 500109 3*0 500009 40600b 2*0 702208 4*0 40600d 6*0 e2701001 3*0 714000 540409 0
  //   428401 480000 3*0 500109 4*0 40600b 2*0 702208 4*0 40600d 6*0 e2701001 3*0 714000 2*0 428401 d00c01
  //   3*0 500109 20500109 2*0 500039 40600b 2*0 702208 80702208 3*0 40600d 6*0 e2701001 6*0 428401 d00c01
  //   7*0 500049 40600b 7*0 40600d 6*0 e2701001 6*0 428401 d00c01 3*0 500109 3*0 500059 40600b 7*0 40600d
  //   6*0 e2701001 3*0 714000 2*0 428401 4*0 500109 4*0 40600b 7*0 40600d 6*0 e2701001 3*0 714000 2*0
  //   428401 c00c01 7*0 500089 40600b 7*0 40600d 6*0 e2701001 3*0 714000 2*0 428401 c00c01 7*0 500099
  //   40600b 7*0 40600d 6*0 e2701001 3*0 714000 2*0 428401 c00c01 3*0 500109 3*0 500009 40600b 2*0 702208
  //   4*0 40600d 10*0 714000 540409 0 428401 480000 3*0 500109 4*0 40600b 2*0 702208 4*0 40600d 10*0
  //   714000 2*0 428401 d00c01 3*0 500109 20500109 2*0 500039 40600b 2*0 702208 80702208 3*0 40600d 13*0
  //   428401 d00c01 7*0 500049 40600b 7*0 40600d 13*0 428401 d00c01 3*0 500109 3*0 500059 40600b 7*0
  //   40600d 10*0 714000 2*0 428401 4*0 500109 4*0 40600b 7*0 40600d 10*0 714000 2*0 428401 c00c01 7*0
  //   500089 40600b 7*0 40600d 10*0 714000 2*0 428401 c00c01 7*0 500099 40600b 7*0 40600d 10*0 714000 2*0
  //   428401 c00c01 3*0 500109 3*0 500009 40600b 2*0 702208 4*0 40600d 10*0 714000 540409 0 428401 480000
  //   3*0 500109 4*0 40600b 2*0 702208 4*0 40600d 10*0 714000 2*0 428401 d00c01 3*0 500109 20500109 2*0
  //   500039 40600b 2*0 702208 80702208 3*0 40600d 13*0 428401 d00c01 7*0 500049 40600b 7*0 40600d 13*0
  //   428401 d00c01 3*0 500109 3*0 500059 40600b 7*0 40600d 10*0 714000 2*0 428401 4*0 500109 4*0 40600b
  //   7*0 40600d 10*0 714000 2*0 428401 c00c01 7*0 500089 40600b 7*0 40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
endmodule

module LoadUnit (
  input  [31:0] din,
  input  [1:0] off,
  input  [2:0] f3,
  output [31:0] v
);

  wire [31:0] bit_extender_2_out, bit_extender_4_out, sb, sh16, x;

  Shifter #(.width(32), .shift("lr")) shifter_1 (.in(din), .\dist ({off, 3'b000}), .out(x));
  assign sb = {{24{x[7]}}, x[7:0]};  // Bit_Extender bit_extender_1
  assign bit_extender_2_out = {{24{1'b0}}, x[7:0]};  // Bit_Extender bit_extender_2
  assign sh16 = {{16{x[15]}}, x[15:0]};  // Bit_Extender bit_extender_3
  assign bit_extender_4_out = {{16{1'b0}}, x[15:0]};  // Bit_Extender bit_extender_4
  Multiplexer #(.width(32), .select(3)) multiplexer_1 (
    .in0(sb), .in1(sh16), .in2(x), .in3(x), .in4(bit_extender_2_out), .in5(bit_extender_4_out), .in6(x),
    .in7(x), .out(v), .sel(f3));

  // Other names for the same wires on the sheet: sh[4:3] = off
endmodule

module StoreUnit (
  input  [31:0] old,
  input  [31:0] wd,
  input  [1:0] off,
  input  [2:0] f3,
  output [31:0] \new 
);

  wire [31:0] and_2_out, ins, multiplexer_1_out, not_1_out, shifter_2_out, wds;

  Multiplexer #(.width(32), .select(2)) multiplexer_1 (
    .in0(32'hff), .in1(32'hffff), .in2({32{1'b1}}), .in3({32{1'b1}}), .out(multiplexer_1_out), .sel(f3[1:0]));
  Shifter #(.width(32), .shift("ll")) shifter_1 (.in(wd), .\dist ({off, 3'b000}), .out(wds));
  Shifter #(.width(32), .shift("ll")) shifter_2 (.in(multiplexer_1_out), .\dist ({off, 3'b000}), .out(shifter_2_out));
  assign not_1_out = ~shifter_2_out;  // NOT_Gate not_1, 32 bits wide
  assign ins = wds & shifter_2_out;  // AND_Gate and_1, 32 bits wide
  assign and_2_out = old & not_1_out;  // AND_Gate and_2, 32 bits wide
  assign \new  = and_2_out | ins;  // OR_Gate or_1, 32 bits wide

  // Other names for the same wires on the sheet: sz[1:0] = f3[1:0]; sh[4:3] = off
endmodule

module MulDiv (
  input  [31:0] a,
  input  [31:0] b,
  input  [2:0] f3,
  output [31:0] y
);

  wire bz;
  wire [31:0] asx, divider_1_out, divider_2_out, hiss, hisu, hiuu, lo, multiplexer_3_out, multiplexer_4_out,
       qu2, rs, ru, ru2;

  Multiplier #(.width(32), .mode("unsigned")) multiplier_1 (.a(a), .b(b), .out(lo), .cout(hiuu));  // open: cin
  Multiplier #(.width(32), .mode("twosComplement")) multiplier_2 (.a(a), .b(b), .cout(hiss));  // open: out, cin
  Multiplier #(.width(32), .mode("signedUnsigned")) multiplier_3 (.a(a), .b(b), .cout(hisu));  // open: out, cin
  Divider #(.width(32), .mode("unsigned")) divider_1 (.a(a), .b(b), .out(divider_1_out), .upper({32{1'b0}}), .rem(ru));
  Comparator #(.width(32), .mode("unsigned")) comparator_1 (.a(b), .b({32{1'b0}}), .eq(bz));  // open: gt, lt
  assign asx = {{31{a[31]}}, a[31]};  // Bit_Extender bit_extender_1
  Multiplexer #(.width(32), .select(1)) multiplexer_1 (.in0(divider_1_out), .in1({32{1'b1}}), .out(qu2), .sel(bz));
  Multiplexer #(.width(32), .select(1)) multiplexer_2 (.in0(ru), .in1(a), .out(ru2), .sel(bz));
  Divider #(.width(32), .mode("twosComplement")) divider_2 (.a(a), .b(b), .out(divider_2_out), .upper(asx), .rem(rs));
  Multiplexer #(.width(32), .select(1)) multiplexer_3 (
    .in0(divider_2_out), .in1({32{1'b1}}), .out(multiplexer_3_out), .sel(bz));
  Multiplexer #(.width(32), .select(1)) multiplexer_4 (.in0(rs), .in1(a), .out(multiplexer_4_out), .sel(bz));
  Multiplexer #(.width(32), .select(3)) multiplexer_5 (
    .in0(lo), .in1(hiss), .in2(hisu), .in3(hiuu), .in4(multiplexer_3_out), .in5(qu2),
    .in6(multiplexer_4_out), .in7(ru2), .out(y), .sel(f3));
endmodule

module InstrDecode (
  input  [31:0] instr,
  output [2:0] f3,
  output [4:0] rd,
  output [4:0] rs1,
  output [4:0] rs2
);


  assign f3 = instr[14:12];
  assign rd = instr[11:7];
  assign rs1 = instr[19:15];
  assign rs2 = instr[24:20];
endmodule

module MainControl (
  input  [31:0] instr,
  output [3:0] ALUOp,
  output [1:0] ASel,
  output BSel,
  output Branch,
  output Halt,
  output [2:0] ImmSel,
  output Jal,
  output Jalr,
  output MemRead,
  output MemWrite,
  output RegWrite,
  output [2:0] ResSel
);

  wire [31:20] ctrl;

  Control control_1 (
    .instr(instr),
    .ctrl({ctrl, Halt, Jalr, Jal, Branch, ImmSel, ResSel, MemWrite, MemRead, ALUOp, BSel, ASel, RegWrite}));

  // Other names for the same wires on the sheet: ctrl[19:0] = {Halt, Jalr, Jal, Branch, ImmSel, ResSel, MemWrite, MemRead, ALUOp, BSel, ASel, RegWrite}
endmodule

module PerfCounters (
  input  clk,
  output [31:0] cycles
);

  wire [31:0] adder_1_out;

  Adder #(.width(32)) adder_1 (.a(cycles), .b(32'h1), .out(adder_1_out));  // open: cin, cout
  Register #(.width(32)) register_1 (.D(adder_1_out), .clk(clk), .Q(cycles));  // open: en, clr
endmodule
